// Logisim project cpu.circ as structural Verilog: 30 circuits, main circuit main
module main (
  input  reset,
  output overflow,
  output isWrong
);

  wire alu_enable, alu_eq, alu_gt, alu_ls, alu_operation, clock_1_out, pc_addr_select, pc_clock, pc_enable,
       ram_read, ram_write, reg_write;
  wire [2:0] reg_in_addr, reg_out_addr1, reg_out_addr2;
  wire [9:0] instruction_register_1_pc_address, pc_addr, ram_addr;
  wire [15:0] alu_in1, alu_in2, alu_out_val, Instruction, ram_in_val, ram_out, reg_in_val, reg_out_val1,
       reg_out_val2;

  Clock clock_1 (.out(clock_1_out));
  // Probe on ram_addr
  // Probe on ram_in_val
  // Probe on pc_addr
  // Probe on ram_out
  _10x10_from_8x8 u_10x10_from_8x8_1 (
    .address_10bit(ram_addr), .data_input(ram_in_val), .data_output(ram_out), .enable_write(ram_write),
    .reset(reset), .clock(clock_1_out), .enable_read(ram_read));
  // Probe on pc_addr
  // Probe on reg_in_addr
  // Probe on reg_in_val
  control_unit control_unit_1 (
    .instruction(Instruction), .clock(clock_1_out), .reset(reset), .ram_out(ram_out), .alu_gt(alu_gt),
    .alu_ls(alu_ls), .alu_eq(alu_eq), .alu_out_value(alu_out_val), .reg_out_val1(reg_out_val1),
    .reg_out_val2(reg_out_val2), .reg_write(reg_write), .alu_enable(alu_enable), .ram_in_value(ram_in_val),
    .alu_op(alu_operation), .reg_in_value(reg_in_val), .pc_clock(pc_clock), .alu_in1(alu_in1),
    .reg_in_addr(reg_in_addr), .pc_addr_select(pc_addr_select), .RAM_READ(ram_read), .pc_enable(pc_enable),
    .reg_out_addr1(reg_out_addr1), .alu_in2(alu_in2), .RAM_WRITE(ram_write), .pc_addr(pc_addr),
    .reg_out_addr2(reg_out_addr2), .ram_addr(ram_addr));
  instruction_register instruction_register_1 (
    .JUMP_ADDRESS(pc_addr), .ADDR_SELECT(pc_addr_select), .PC_ADDRESS(instruction_register_1_pc_address),
    .Enable(pc_enable), .Clock(clock_1_out), .Clear(reset));
  register_file register_file_1 (
    .Data(reg_in_val), .ReadReg1(reg_out_addr1), .ReadReg2(reg_out_addr2), .RegWrite(reg_write),
    .clk(clock_1_out), .reset(reset), .RegOut1(reg_out_val1), .RegOut2(reg_out_val2), .WriteReg(reg_in_addr));
  // Probe on instruction_register_1_pc_address
  // Probe on reg_out_val1
  // Probe on reg_out_val2
  // Probe on reg_out_addr1
  // Probe on reg_out_addr2
  // Probe on Instruction
  ROM #(.addrWidth(10), .dataWidth(16)) rom_1 (
    .addr(instruction_register_1_pc_address), .data(Instruction));  // open: sel
  // Probe on alu_in2
  // Probe on alu_in1
  alu alu_1 (
    .a(alu_in1), .b(alu_in2), ._0and_1add(alu_operation), .enable(alu_enable), .result(alu_out_val),
    .overflow(overflow), .isWrong(isWrong), .gt(alu_gt), .lt(alu_ls), .eq(alu_eq));
  // Probe on alu_out_val

  // Notes on the sheet:
  //   Instruction Memory
  //   contents of rom_1 (hex, n*v repeats v):
  //   1b09 ac00 2303 2801 2 f968 f02c ebfd 8400 fc4d a401
endmodule

module register_file (
  input  [15:0] Data,
  input  [2:0] WriteReg,
  input  [2:0] ReadReg1,
  input  [2:0] ReadReg2,
  input  RegWrite,
  input  clk,
  input  reset,
  output [15:0] RegOut1,
  output [15:0] RegOut2
);

  wire and_1_out, and_2_out, and_3_out, and_4_out, and_5_out, and_6_out, and_7_out, and_8_out,
       decoder_1_out0, decoder_1_out1, decoder_1_out2, decoder_1_out3, decoder_1_out4, decoder_1_out5,
       decoder_1_out6, decoder_1_out7;
  wire [15:0] r0_output, r1_output, r2_output, r3_output, r4_output, r5_output, r6_output, r7_output;

  Decoder #(.select(3), .enable("false")) decoder_1 (
    .out0(decoder_1_out0), .out1(decoder_1_out1), .out2(decoder_1_out2), .out3(decoder_1_out3),
    .out4(decoder_1_out4), .out5(decoder_1_out5), .out6(decoder_1_out6), .out7(decoder_1_out7), .sel(WriteReg));
  // Probe on Data
  and and_1 (and_1_out, decoder_1_out4, RegWrite);
  and and_2 (and_2_out, decoder_1_out0, RegWrite);
  and and_3 (and_3_out, decoder_1_out5, RegWrite);
  and and_4 (and_4_out, decoder_1_out1, RegWrite);
  and and_5 (and_5_out, decoder_1_out6, RegWrite);
  and and_6 (and_6_out, decoder_1_out2, RegWrite);
  and and_7 (and_7_out, decoder_1_out7, RegWrite);
  and and_8 (and_8_out, decoder_1_out3, RegWrite);
  flip_flop_store r0 (.\input (Data), .write_enable(and_2_out), .reset(reset), .clock(clk), .\output (r0_output));
  flip_flop_store r1 (.\input (Data), .write_enable(and_4_out), .reset(reset), .clock(clk), .\output (r1_output));
  flip_flop_store r2 (.\input (Data), .write_enable(and_6_out), .reset(reset), .clock(clk), .\output (r2_output));
  flip_flop_store r3 (.\input (Data), .write_enable(and_8_out), .reset(reset), .clock(clk), .\output (r3_output));
  flip_flop_store r4 (.\input (Data), .write_enable(and_1_out), .reset(reset), .clock(clk), .\output (r4_output));
  flip_flop_store r5 (.\input (Data), .write_enable(and_3_out), .reset(reset), .clock(clk), .\output (r5_output));
  flip_flop_store r6 (.\input (Data), .write_enable(and_5_out), .reset(reset), .clock(clk), .\output (r6_output));
  flip_flop_store r7 (.\input (Data), .write_enable(and_7_out), .reset(reset), .clock(clk), .\output (r7_output));
  // Probe on r0_output
  // Probe on r4_output
  // Probe on r2_output
  // Probe on r5_output
  // Probe on r6_output
  // Probe on r7_output
  // Probe on r1_output
  // Probe on r3_output
  Multiplexer #(.select(3), .width(16), .enable("false")) multiplexer_1 (
    .in0(r0_output), .in1(r1_output), .in2(r2_output), .in3(r3_output), .in4(r4_output), .in5(r5_output),
    .in6(r6_output), .in7(r7_output), .out(RegOut1), .sel(ReadReg1));
  Multiplexer #(.select(3), .width(16), .enable("false")) multiplexer_2 (
    .in0(r0_output), .in1(r1_output), .in2(r2_output), .in3(r3_output), .in4(r4_output), .in5(r5_output),
    .in6(r6_output), .in7(r7_output), .out(RegOut2), .sel(ReadReg2));
endmodule

module instruction_register (
  input  [9:0] JUMP_ADDRESS,
  input  ADDR_SELECT,
  input  Enable,
  input  Clock,
  input  Clear,
  output [9:0] PC_ADDRESS
);

  wire [9:0] adder_1_out, multiplexer_1_out;

  Multiplexer #(.width(10), .enable("false")) multiplexer_1 (
    .in0(10'h1), .in1(JUMP_ADDRESS), .out(multiplexer_1_out), .sel(ADDR_SELECT));
  Adder #(.width(10)) adder_1 (.a(multiplexer_1_out), .b(PC_ADDRESS), .out(adder_1_out));  // open: cin, cout
  Register #(.width(10)) register_1 (.D(adder_1_out), .en(Enable), .Q(PC_ADDRESS), .clk(Clock), .clr(Clear));
  // Probe on adder_1_out
endmodule

module flip_flop_store (
  input  [15:0] \input ,
  input  write_enable,
  input  reset,
  input  clock,
  output [15:0] \output 
);

  wire and_1_out, and_2_out, and_3_out, and_4_out, and_5_out, and_6_out, and_7_out, and_8_out, and_9_out,
       and_10_out, and_11_out, and_12_out, and_13_out, and_14_out, and_15_out, and_16_out, and_17_out,
       and_18_out, and_19_out, and_20_out, and_21_out, and_22_out, and_23_out, and_24_out, and_25_out,
       and_26_out, and_27_out, and_28_out, and_29_out, and_30_out, and_31_out, and_32_out, and_33_out,
       and_34_out, and_35_out, and_36_out, and_37_out, and_38_out, and_39_out, and_40_out, and_41_out,
       and_42_out, and_43_out, and_44_out, and_45_out, and_46_out, and_47_out, and_48_out, and_49_out,
       and_50_out, and_51_out, and_52_out, and_53_out, and_54_out, and_55_out, and_56_out, and_57_out,
       and_58_out, and_59_out, and_60_out, and_61_out, and_62_out, and_63_out, and_64_out, and_65_out,
       and_66_out, and_67_out, and_68_out, and_69_out, and_70_out, and_71_out, and_72_out, and_73_out,
       and_74_out, and_75_out, and_76_out, and_77_out, and_78_out, and_79_out, and_80_out, not_1_out,
       not_2_out, not_3_out, not_4_out, not_5_out, not_6_out, not_7_out, not_8_out, not_9_out, not_10_out,
       not_11_out, not_12_out, not_13_out, not_14_out, not_15_out, not_16_out, not_17_out, not_18_out,
       not_19_out, not_20_out, not_21_out, not_22_out, not_23_out, not_24_out, not_25_out, not_26_out,
       not_27_out, not_28_out, not_29_out, not_30_out, not_31_out, not_32_out, not_33_out, not_34_out,
       not_35_out, not_36_out, not_37_out, not_38_out, not_39_out, not_40_out, not_41_out, not_42_out,
       not_43_out, not_44_out, not_45_out, not_46_out, not_47_out, not_48_out, not_49_out, not_50_out,
       not_51_out, not_52_out, not_53_out, not_54_out, not_55_out, not_56_out, not_57_out, not_58_out,
       not_59_out, not_60_out, not_61_out, not_62_out, not_63_out, not_64_out, not_65_out, not_66_out,
       not_67_out, not_68_out, not_69_out, not_70_out, not_71_out, not_72_out, not_73_out, not_74_out,
       not_75_out, not_76_out, not_77_out, not_78_out, not_79_out, not_80_out, not_81_out, not_82_out,
       not_83_out, not_84_out, not_85_out, not_86_out, not_87_out, not_88_out, not_89_out, not_90_out,
       not_91_out, not_92_out, not_93_out, not_94_out, not_95_out, not_96_out, not_97_out, not_98_out,
       not_99_out, not_100_out, not_101_out, not_102_out, not_103_out, not_104_out, not_105_out, not_106_out,
       not_107_out, not_108_out, not_109_out, not_110_out, not_111_out, not_112_out, not_113_out,
       not_114_out, not_115_out, not_116_out, not_117_out, not_118_out, not_119_out, not_120_out,
       not_121_out, not_122_out, not_123_out, not_124_out, not_125_out, not_126_out, not_127_out,
       not_128_out, not_129_out, or_1_out, or_2_out, or_3_out, or_4_out, or_5_out, or_6_out, or_7_out,
       or_8_out, or_9_out, or_10_out, or_11_out, or_12_out, or_13_out, or_14_out, or_15_out, or_16_out,
       or_17_out, or_18_out, or_19_out, or_20_out, or_21_out, or_22_out, or_23_out, or_24_out, or_25_out,
       or_26_out, or_27_out, or_28_out, or_29_out, or_30_out, or_31_out, or_32_out, or_33_out, or_34_out,
       or_35_out, or_36_out, or_37_out, or_38_out, or_39_out, or_40_out, or_41_out, or_42_out, or_43_out,
       or_44_out, or_45_out, or_46_out, or_47_out, or_48_out, or_49_out, or_50_out, or_51_out, or_52_out,
       or_53_out, or_54_out, or_55_out, or_56_out, or_57_out, or_58_out, or_59_out, or_60_out, or_61_out,
       or_62_out, or_63_out, or_64_out;
  wire [15:0] multiplexer_1_out;

  Multiplexer #(.width(16), .enable("false")) multiplexer_1 (
    .in0(\output ), .in1(\input ), .out(multiplexer_1_out), .sel(write_enable));
  not not_1 (not_1_out, multiplexer_1_out[0]);
  not not_2 (not_2_out, multiplexer_1_out[1]);
  not not_3 (not_3_out, multiplexer_1_out[2]);
  not not_4 (not_4_out, multiplexer_1_out[3]);
  not not_5 (not_5_out, multiplexer_1_out[4]);
  not not_6 (not_6_out, multiplexer_1_out[5]);
  not not_7 (not_7_out, multiplexer_1_out[6]);
  not not_8 (not_8_out, multiplexer_1_out[7]);
  not not_9 (not_9_out, multiplexer_1_out[8]);
  not not_10 (not_10_out, multiplexer_1_out[9]);
  not not_11 (not_11_out, multiplexer_1_out[10]);
  not not_12 (not_12_out, multiplexer_1_out[11]);
  not not_13 (not_13_out, multiplexer_1_out[12]);
  not not_14 (not_14_out, multiplexer_1_out[13]);
  not not_15 (not_15_out, multiplexer_1_out[14]);
  not not_16 (not_16_out, multiplexer_1_out[15]);
  and and_1 (and_1_out, multiplexer_1_out[0], clock);
  and and_2 (and_2_out, clock, not_1_out);
  and and_3 (and_3_out, multiplexer_1_out[1], clock);
  and and_4 (and_4_out, clock, not_2_out);
  and and_5 (and_5_out, multiplexer_1_out[2], clock);
  and and_6 (and_6_out, clock, not_3_out);
  and and_7 (and_7_out, multiplexer_1_out[3], clock);
  and and_8 (and_8_out, clock, not_4_out);
  and and_9 (and_9_out, multiplexer_1_out[4], clock);
  and and_10 (and_10_out, clock, not_5_out);
  and and_11 (and_11_out, multiplexer_1_out[5], clock);
  and and_12 (and_12_out, clock, not_6_out);
  and and_13 (and_13_out, multiplexer_1_out[6], clock);
  and and_14 (and_14_out, clock, not_7_out);
  and and_15 (and_15_out, multiplexer_1_out[7], clock);
  and and_16 (and_16_out, clock, not_8_out);
  and and_17 (and_17_out, multiplexer_1_out[8], clock);
  and and_18 (and_18_out, clock, not_9_out);
  and and_19 (and_19_out, multiplexer_1_out[9], clock);
  and and_20 (and_20_out, clock, not_10_out);
  and and_21 (and_21_out, multiplexer_1_out[10], clock);
  and and_22 (and_22_out, clock, not_11_out);
  and and_23 (and_23_out, multiplexer_1_out[11], clock);
  and and_24 (and_24_out, clock, not_12_out);
  and and_25 (and_25_out, multiplexer_1_out[12], clock);
  and and_26 (and_26_out, clock, not_13_out);
  and and_27 (and_27_out, multiplexer_1_out[13], clock);
  and and_28 (and_28_out, clock, not_14_out);
  and and_29 (and_29_out, multiplexer_1_out[14], clock);
  and and_30 (and_30_out, clock, not_15_out);
  and and_31 (and_31_out, multiplexer_1_out[15], clock);
  and and_32 (and_32_out, clock, not_16_out);
  or or_1 (or_1_out, and_1_out, and_33_out);
  not not_17 (not_17_out, or_1_out);
  not not_18 (not_18_out, or_2_out);
  or or_2 (or_2_out, not_17_out, and_2_out);
  or or_3 (or_3_out, and_3_out, and_34_out);
  not not_19 (not_19_out, or_3_out);
  not not_20 (not_20_out, or_4_out);
  or or_4 (or_4_out, not_19_out, and_4_out);
  not not_21 (not_21_out, or_5_out);
  or or_5 (or_5_out, and_5_out, and_35_out);
  or or_6 (or_6_out, not_21_out, and_6_out);
  not not_22 (not_22_out, or_6_out);
  not not_23 (not_23_out, or_7_out);
  or or_7 (or_7_out, and_7_out, and_36_out);
  or or_8 (or_8_out, not_23_out, and_8_out);
  not not_24 (not_24_out, or_8_out);
  not not_25 (not_25_out, or_9_out);
  or or_9 (or_9_out, and_9_out, and_37_out);
  not not_26 (not_26_out, or_10_out);
  or or_10 (or_10_out, not_25_out, and_10_out);
  not not_27 (not_27_out, or_11_out);
  or or_11 (or_11_out, and_11_out, and_38_out);
  not not_28 (not_28_out, or_12_out);
  or or_12 (or_12_out, not_27_out, and_12_out);
  not not_29 (not_29_out, or_13_out);
  or or_13 (or_13_out, and_13_out, and_39_out);
  or or_14 (or_14_out, not_29_out, and_14_out);
  not not_30 (not_30_out, or_14_out);
  not not_31 (not_31_out, or_15_out);
  or or_15 (or_15_out, and_15_out, and_40_out);
  not not_32 (not_32_out, or_16_out);
  or or_16 (or_16_out, not_31_out, and_16_out);
  not not_33 (not_33_out, or_17_out);
  or or_17 (or_17_out, and_17_out, and_41_out);
  or or_18 (or_18_out, not_33_out, and_18_out);
  not not_34 (not_34_out, or_18_out);
  not not_35 (not_35_out, or_19_out);
  or or_19 (or_19_out, and_19_out, and_42_out);
  not not_36 (not_36_out, or_20_out);
  or or_20 (or_20_out, not_35_out, and_20_out);
  not not_37 (not_37_out, or_21_out);
  or or_21 (or_21_out, and_21_out, and_43_out);
  or or_22 (or_22_out, not_37_out, and_22_out);
  not not_38 (not_38_out, or_22_out);
  not not_39 (not_39_out, or_23_out);
  or or_23 (or_23_out, and_23_out, and_44_out);
  not not_40 (not_40_out, or_24_out);
  or or_24 (or_24_out, not_39_out, and_24_out);
  not not_41 (not_41_out, or_25_out);
  or or_25 (or_25_out, and_25_out, and_45_out);
  or or_26 (or_26_out, not_41_out, and_26_out);
  not not_42 (not_42_out, or_26_out);
  or or_27 (or_27_out, and_27_out, and_46_out);
  not not_43 (not_43_out, or_27_out);
  or or_28 (or_28_out, not_43_out, and_28_out);
  not not_44 (not_44_out, or_28_out);
  not not_45 (not_45_out, or_29_out);
  or or_29 (or_29_out, and_29_out, and_47_out);
  not not_46 (not_46_out, or_30_out);
  or or_30 (or_30_out, not_45_out, and_30_out);
  not not_47 (not_47_out, or_31_out);
  or or_31 (or_31_out, and_31_out, and_48_out);
  or or_32 (or_32_out, not_47_out, and_32_out);
  not not_48 (not_48_out, or_32_out);
  not not_49 (not_49_out, reset);
  and and_33 (and_33_out, not_49_out, not_18_out);
  not not_50 (not_50_out, and_33_out);
  not not_51 (not_51_out, reset);
  and and_34 (and_34_out, not_51_out, not_20_out);
  not not_52 (not_52_out, and_34_out);
  not not_53 (not_53_out, reset);
  and and_35 (and_35_out, not_53_out, not_22_out);
  not not_54 (not_54_out, and_35_out);
  not not_55 (not_55_out, reset);
  and and_36 (and_36_out, not_55_out, not_24_out);
  not not_56 (not_56_out, and_36_out);
  not not_57 (not_57_out, reset);
  and and_37 (and_37_out, not_57_out, not_26_out);
  not not_58 (not_58_out, and_37_out);
  not not_59 (not_59_out, reset);
  and and_38 (and_38_out, not_59_out, not_28_out);
  not not_60 (not_60_out, and_38_out);
  not not_61 (not_61_out, reset);
  and and_39 (and_39_out, not_61_out, not_30_out);
  not not_62 (not_62_out, and_39_out);
  not not_63 (not_63_out, reset);
  and and_40 (and_40_out, not_63_out, not_32_out);
  not not_64 (not_64_out, and_40_out);
  not not_65 (not_65_out, reset);
  and and_41 (and_41_out, not_65_out, not_34_out);
  not not_66 (not_66_out, and_41_out);
  not not_67 (not_67_out, reset);
  and and_42 (and_42_out, not_67_out, not_36_out);
  not not_68 (not_68_out, and_42_out);
  not not_69 (not_69_out, reset);
  and and_43 (and_43_out, not_69_out, not_38_out);
  not not_70 (not_70_out, and_43_out);
  not not_71 (not_71_out, reset);
  and and_44 (and_44_out, not_71_out, not_40_out);
  not not_72 (not_72_out, and_44_out);
  not not_73 (not_73_out, reset);
  and and_45 (and_45_out, not_73_out, not_42_out);
  not not_74 (not_74_out, and_45_out);
  not not_75 (not_75_out, reset);
  and and_46 (and_46_out, not_75_out, not_44_out);
  not not_76 (not_76_out, and_46_out);
  not not_77 (not_77_out, reset);
  and and_47 (and_47_out, not_77_out, not_46_out);
  not not_78 (not_78_out, and_47_out);
  not not_79 (not_79_out, reset);
  and and_48 (and_48_out, not_79_out, not_48_out);
  not not_80 (not_80_out, and_48_out);
  not not_81 (not_81_out, clock);
  and and_49 (and_49_out, and_33_out, not_81_out);
  or or_33 (or_33_out, and_49_out, \output [0]);
  or or_34 (or_34_out, not_82_out, and_50_out);
  and and_50 (and_50_out, not_81_out, not_50_out);
  and and_51 (and_51_out, and_34_out, not_81_out);
  or or_35 (or_35_out, and_51_out, \output [1]);
  or or_36 (or_36_out, not_85_out, and_52_out);
  and and_52 (and_52_out, not_81_out, not_52_out);
  and and_53 (and_53_out, and_35_out, not_81_out);
  or or_37 (or_37_out, and_53_out, \output [2]);
  or or_38 (or_38_out, not_88_out, and_54_out);
  and and_54 (and_54_out, not_81_out, not_54_out);
  and and_55 (and_55_out, and_36_out, not_81_out);
  or or_39 (or_39_out, and_55_out, \output [3]);
  or or_40 (or_40_out, not_91_out, and_56_out);
  and and_56 (and_56_out, not_81_out, not_56_out);
  and and_57 (and_57_out, and_37_out, not_81_out);
  or or_41 (or_41_out, and_57_out, \output [4]);
  or or_42 (or_42_out, not_94_out, and_58_out);
  and and_58 (and_58_out, not_81_out, not_58_out);
  and and_59 (and_59_out, and_38_out, not_81_out);
  or or_43 (or_43_out, and_59_out, \output [5]);
  or or_44 (or_44_out, not_97_out, and_60_out);
  and and_60 (and_60_out, not_81_out, not_60_out);
  and and_61 (and_61_out, and_39_out, not_81_out);
  or or_45 (or_45_out, and_61_out, \output [6]);
  or or_46 (or_46_out, not_100_out, and_62_out);
  and and_62 (and_62_out, not_81_out, not_62_out);
  and and_63 (and_63_out, and_40_out, not_81_out);
  or or_47 (or_47_out, and_63_out, \output [7]);
  or or_48 (or_48_out, not_103_out, and_64_out);
  and and_64 (and_64_out, not_81_out, not_64_out);
  and and_65 (and_65_out, and_41_out, not_81_out);
  or or_49 (or_49_out, and_65_out, \output [8]);
  or or_50 (or_50_out, not_106_out, and_66_out);
  and and_66 (and_66_out, not_81_out, not_66_out);
  and and_67 (and_67_out, and_42_out, not_81_out);
  or or_51 (or_51_out, and_67_out, \output [9]);
  or or_52 (or_52_out, not_109_out, and_68_out);
  and and_68 (and_68_out, not_81_out, not_68_out);
  and and_69 (and_69_out, and_43_out, not_81_out);
  or or_53 (or_53_out, and_69_out, \output [10]);
  or or_54 (or_54_out, not_112_out, and_70_out);
  and and_70 (and_70_out, not_81_out, not_70_out);
  and and_71 (and_71_out, and_44_out, not_81_out);
  or or_55 (or_55_out, and_71_out, \output [11]);
  or or_56 (or_56_out, not_115_out, and_72_out);
  and and_72 (and_72_out, not_81_out, not_72_out);
  and and_73 (and_73_out, and_45_out, not_81_out);
  or or_57 (or_57_out, and_73_out, \output [12]);
  or or_58 (or_58_out, not_118_out, and_74_out);
  and and_74 (and_74_out, not_81_out, not_74_out);
  and and_75 (and_75_out, and_46_out, not_81_out);
  or or_59 (or_59_out, and_75_out, \output [13]);
  or or_60 (or_60_out, not_121_out, and_76_out);
  and and_76 (and_76_out, not_81_out, not_76_out);
  and and_77 (and_77_out, and_47_out, not_81_out);
  or or_61 (or_61_out, and_77_out, \output [14]);
  or or_62 (or_62_out, not_124_out, and_78_out);
  and and_78 (and_78_out, not_81_out, not_78_out);
  and and_79 (and_79_out, and_48_out, not_81_out);
  or or_63 (or_63_out, and_79_out, \output [15]);
  or or_64 (or_64_out, not_127_out, and_80_out);
  and and_80 (and_80_out, not_81_out, not_80_out);
  not not_82 (not_82_out, or_33_out);
  not not_83 (not_83_out, reset);
  and and_81 (\output [0], not_83_out, not_84_out);
  not not_84 (not_84_out, or_34_out);
  not not_85 (not_85_out, or_35_out);
  not not_86 (not_86_out, reset);
  and and_82 (\output [1], not_86_out, not_87_out);
  not not_87 (not_87_out, or_36_out);
  not not_88 (not_88_out, or_37_out);
  not not_89 (not_89_out, reset);
  and and_83 (\output [2], not_89_out, not_90_out);
  not not_90 (not_90_out, or_38_out);
  not not_91 (not_91_out, or_39_out);
  not not_92 (not_92_out, reset);
  and and_84 (\output [3], not_92_out, not_93_out);
  not not_93 (not_93_out, or_40_out);
  not not_94 (not_94_out, or_41_out);
  not not_95 (not_95_out, reset);
  and and_85 (\output [4], not_95_out, not_96_out);
  not not_96 (not_96_out, or_42_out);
  not not_97 (not_97_out, or_43_out);
  not not_98 (not_98_out, reset);
  and and_86 (\output [5], not_98_out, not_99_out);
  not not_99 (not_99_out, or_44_out);
  not not_100 (not_100_out, or_45_out);
  not not_101 (not_101_out, reset);
  and and_87 (\output [6], not_101_out, not_102_out);
  not not_102 (not_102_out, or_46_out);
  not not_103 (not_103_out, or_47_out);
  not not_104 (not_104_out, reset);
  and and_88 (\output [7], not_104_out, not_105_out);
  not not_105 (not_105_out, or_48_out);
  not not_106 (not_106_out, or_49_out);
  not not_107 (not_107_out, reset);
  and and_89 (\output [8], not_107_out, not_108_out);
  not not_108 (not_108_out, or_50_out);
  not not_109 (not_109_out, or_51_out);
  not not_110 (not_110_out, reset);
  and and_90 (\output [9], not_110_out, not_111_out);
  not not_111 (not_111_out, or_52_out);
  not not_112 (not_112_out, or_53_out);
  not not_113 (not_113_out, reset);
  and and_91 (\output [10], not_113_out, not_114_out);
  not not_114 (not_114_out, or_54_out);
  not not_115 (not_115_out, or_55_out);
  not not_116 (not_116_out, reset);
  and and_92 (\output [11], not_116_out, not_117_out);
  not not_117 (not_117_out, or_56_out);
  not not_118 (not_118_out, or_57_out);
  not not_119 (not_119_out, reset);
  and and_93 (\output [12], not_119_out, not_120_out);
  not not_120 (not_120_out, or_58_out);
  not not_121 (not_121_out, or_59_out);
  not not_122 (not_122_out, reset);
  and and_94 (\output [13], not_122_out, not_123_out);
  not not_123 (not_123_out, or_60_out);
  not not_124 (not_124_out, or_61_out);
  not not_125 (not_125_out, reset);
  and and_95 (\output [14], not_125_out, not_126_out);
  not not_126 (not_126_out, or_62_out);
  not not_127 (not_127_out, or_63_out);
  not not_128 (not_128_out, reset);
  and and_96 (\output [15], not_128_out, not_129_out);
  not not_129 (not_129_out, or_64_out);
endmodule

// ALU
module alu (
  input  [15:0] a,
  input  [15:0] b,
  input  _0and_1add,
  input  enable,
  output [15:0] result,
  output overflow,
  output isWrong,
  output gt,
  output lt,
  output eq
);

  wire [15:0] adder_1_sum, and_out, multiplexer_1_out, multiplexer_2_out;

  Multiplexer #(.width(16), .enable("false")) multiplexer_1 (
    .in0(multiplexer_1_out), .in1(a), .out(multiplexer_1_out), .sel(enable));
  Multiplexer #(.width(16), .enable("false")) multiplexer_2 (
    .in0(multiplexer_2_out), .in1(b), .out(multiplexer_2_out), .sel(enable));
  // Probe on multiplexer_1_out
  // Probe on multiplexer_2_out
  // Probe on multiplexer_1_out
  assign and_out = multiplexer_1_out & multiplexer_2_out;  // AND_Gate and, 16 bits wide
  // Probe on adder_1_sum
  adder adder_1 (
    .a(multiplexer_1_out), .b(multiplexer_2_out), .sum(adder_1_sum), .overflow(overflow), .isWrong(isWrong));
  comparator comparator_1 (.a(multiplexer_1_out), .b(multiplexer_2_out), .gt(gt), .lt(lt), .eq(eq));
  Multiplexer #(.width(16), .enable("false")) multiplexer_3 (
    .in0(and_out), .in1(adder_1_sum), .out(result), .sel(_0and_1add));
endmodule

module control_unit (
  input  [15:0] instruction,
  input  clock,
  input  reset,
  input  [15:0] ram_out,
  input  alu_gt,
  input  alu_ls,
  input  alu_eq,
  input  [15:0] alu_out_value,
  input  [15:0] reg_out_val1,
  input  [15:0] reg_out_val2,
  output reg_write,
  output alu_enable,
  output [15:0] ram_in_value,
  output alu_op,
  output [15:0] reg_in_value,
  output pc_clock,
  output [15:0] alu_in1,
  output [2:0] reg_in_addr,
  output pc_addr_select,
  output RAM_READ,
  output pc_enable,
  output [2:0] reg_out_addr1,
  output [15:0] alu_in2,
  output RAM_WRITE,
  output [9:0] pc_addr,
  output [2:0] reg_out_addr2,
  output [9:0] ram_addr
);

  wire ADD, ADDI, ALU_ENABLE1, ALU_ENABLE2, ALU_ENABLE3, ALU_ENABLE4, ALU_ENABLE5, AND, ANDI, CMP,
       decoder_1_out0, decoder_1_out1, decoder_1_out2, decoder_1_out3, decoder_1_out4, decoder_1_out5,
       decoder_1_out6, decoder_1_out7, decoder_1_out8, decoder_1_out9, decoder_1_out10, decoder_1_out11,
       decoder_1_out12, decoder_1_out13, decoder_1_out14, decoder_1_out15, decoder_1_out16, decoder_1_out17,
       decoder_1_out18, decoder_1_out19, decoder_1_out20, decoder_1_out21, decoder_1_out22, decoder_1_out23,
       decoder_2_out0, decoder_2_out1, EQ, fetch, GT, J, JA, JAE, JB, JBE, JE, JMP, LD, LS, or_6_out,
       or_7_out, or_8_out, or_9_out, reg_write1, reg_write3, reg_write4, reg_write5, reg_write6, reg_write7,
       REGZ_ENABLE, ST;
  wire [1:1] decoder_1_out31;
  wire [2:0] DEST, SRC1;
  wire [9:0] undriven;
  wire [15:0] regz_in, regz_out;

  addi_state addi_state_1 (
    .src1(SRC1), .reg_out1(reg_out_val1), .regz_out(regz_out), .dest(DEST), .eq(alu_eq),
    .imm(instruction[7:0]), .ls(alu_ls), .gt(alu_gt), .alu_out(alu_out_value), .st___active(ADDI),
    .clock(clock), .reset(reset), .regz_in(regz_in), .regz_enable(REGZ_ENABLE),
    .reg_out_addr1(reg_out_addr1), .alu_in1(alu_in1), .alu_in_2(alu_in2), .alu_op(alu_op),
    .alu_enable(ALU_ENABLE1), .reg_in_add(reg_in_addr), .reg_in(reg_in_value), .reg_write(reg_write3),
    .fetch(fetch));
  Decoder #(.select(5), .enable("false")) decoder_1 (
    .out0(decoder_1_out0), .out1(decoder_1_out1), .out2(decoder_1_out2), .out3(decoder_1_out3),
    .out4(decoder_1_out4), .out5(decoder_1_out5), .out6(decoder_1_out6), .out7(decoder_1_out7),
    .out8(decoder_1_out8), .out9(decoder_1_out9), .out10(decoder_1_out10), .out11(decoder_1_out11),
    .out12(decoder_1_out12), .out13(decoder_1_out13), .out14(decoder_1_out14), .out15(decoder_1_out15),
    .out16(decoder_1_out16), .out17(decoder_1_out17), .out18(decoder_1_out18), .out19(decoder_1_out19),
    .out20(decoder_1_out20), .out21(decoder_1_out21), .out22(decoder_1_out22), .out23(decoder_1_out23),
    .out24(JMP), .out25(JE), .out26(JA), .out27(JAE), .out28(JB), .out29(JBE), .out30(CMP),
    .out31(decoder_1_out31[1]), .sel(instruction[15:11]));
  or or_1 (ADDI, decoder_1_out0, decoder_1_out1, decoder_1_out2, decoder_1_out3, decoder_1_out4, decoder_1_out5, decoder_1_out6, decoder_1_out7);
  // Probe on regz_in
  ld_state ld_state_1 (
    .dest(DEST), .regz_out(regz_out), .ram_out(ram_out), .addr(instruction[9:0]), .st___active(LD),
    .clock(clock), .reset(reset), .reg_in_addr(reg_in_addr), .reg_in(reg_in_value), .regz_en(REGZ_ENABLE),
    .ram_addr(ram_addr), .ram_r_ena(RAM_READ), .regz_in(regz_in), .reg_write(reg_write1), .fetch(fetch));
  add_state add_state_1 (
    .src1(SRC1), .reg_out1(reg_out_val1), .dest(DEST), .regz_out(regz_out), .src2(instruction[2:0]),
    .eq(alu_eq), .reg_out2(reg_out_val2), .ls(alu_ls), .gt(alu_gt), .alu_out(alu_out_value),
    .st___active(ADD), .clock(clock), .reset(reset), .regz_in(regz_in), .regz_enable(REGZ_ENABLE),
    .reg_out_addr1(reg_out_addr1), .reg_out_addr2(reg_out_addr2), .alu_in1(alu_in1), .alu_in_2(alu_in2),
    .alu_op(alu_op), .alu_enable(ALU_ENABLE3), .reg_in_add(reg_in_addr), .reg_in(reg_in_value),
    .reg_write(reg_write5), .fetch(fetch));
  jmp_state jmp_state_1 (
    .address(undriven), .alu_eq(EQ), .alu_ls(LS), .alu_gt(GT), .st___active(JMP), .clock(clock),
    .reset(reset), .pc_enable(pc_enable), .pc_addr(pc_addr), .pc_addr_select(pc_addr_select), .fetch(fetch));
  or or_2 (ANDI, decoder_1_out8, decoder_1_out9, decoder_1_out10, decoder_1_out11, decoder_1_out12, decoder_1_out13, decoder_1_out14, decoder_1_out15);
  // Probe on regz_out
  Register #(.width(16)) REGZ (.D(regz_in), .en(REGZ_ENABLE), .Q(regz_out), .clk(clock), .clr(reset));
  or or_3 (LD, decoder_1_out16, decoder_1_out17, decoder_1_out18, decoder_1_out19);
  or or_4 (ST, decoder_1_out20, decoder_1_out21, decoder_1_out22, decoder_1_out23);
  ja_state ja_state_1 (
    .address(instruction[9:0]), .alu_eq(EQ), .alu_ls(LS), .alu_gt(GT), .st___active(JA), .clock(clock),
    .reset(reset), .pc_enable(pc_enable), .pc_addr(pc_addr), .pc_addr_select(pc_addr_select), .fetch(fetch));
  or or_5 (J, JE, JMP, JBE, JB, JAE, JA);
  st_state st_state_1 (
    .src1(SRC1), .reg_out1(reg_out_val1), .regz_out(regz_out), .ADDRESS(instruction[9:0]), .LD___active(ST),
    .clock(clock), .reset(reset), .reg_out_add1(reg_out_addr1), .regz_in(regz_in), .regz_enable(REGZ_ENABLE),
    .ram_in(ram_in_value), .RAM_ADDR(ram_addr), .RAM_W_ENABLE(RAM_WRITE), .pc_enable(pc_enable),
    .pc_addr_select(pc_addr_select), .fetch_next_inst(fetch));
  andi_state andi_state_1 (
    .src1(SRC1), .reg_out1(reg_out_val1), .regz_out(regz_out), .dest(DEST), .eq(alu_eq),
    .imm(instruction[7:0]), .ls(alu_ls), .gt(alu_gt), .alu_out(alu_out_value), .st___active(ANDI),
    .clock(clock), .reset(reset), .regz_in(regz_in), .regz_enable(REGZ_ENABLE),
    .reg_out_addr1(reg_out_addr1), .alu_in1(alu_in1), .alu_in_2(alu_in2), .alu_op(alu_op),
    .alu_enable(ALU_ENABLE2), .reg_in_add(reg_in_addr), .reg_in(reg_in_value), .reg_write(reg_write4),
    .fetch(fetch));
  Decoder #(.select(2), .enable("false")) decoder_2 (
    .out0(decoder_2_out0), .out1(decoder_2_out1), .out2(ADD), .out3(AND),
    .sel({decoder_1_out31[1], instruction[10]}));
  Register #(.width(1)) u_gt (.D(alu_gt), .en(alu_enable), .Q(GT), .clk(clock), .clr(reset));
  Register #(.width(1)) u_eq (.D(alu_eq), .en(alu_enable), .Q(EQ), .clk(clock), .clr(reset));
  Register #(.width(1)) lt (.D(alu_ls), .en(alu_enable), .Q(LS), .clk(clock), .clr(reset));
  and_state and_state_1 (
    .src1(SRC1), .reg_out1(reg_out_val1), .dest(DEST), .regz_out(regz_out), .src2(instruction[2:0]),
    .eq(alu_eq), .reg_out2(reg_out_val2), .ls(alu_ls), .gt(alu_gt), .alu_out(alu_out_value),
    .st___active(AND), .clock(clock), .reset(reset), .regz_in(regz_in), .regz_enable(REGZ_ENABLE),
    .reg_out_addr1(reg_out_addr1), .reg_out_addr2(reg_out_addr2), .alu_in1(alu_in1), .alu_in_2(alu_in2),
    .alu_op(alu_op), .alu_enable(ALU_ENABLE4), .reg_in_add(reg_in_addr), .reg_in(reg_in_value),
    .reg_write(reg_write6), .fetch(fetch));
  jae_state jae_state_1 (
    .address(instruction[9:0]), .alu_eq(EQ), .alu_ls(LS), .alu_gt(GT), .st___active(JAE), .clock(clock),
    .reset(reset), .pc_enable(pc_enable), .pc_addr(pc_addr), .pc_addr_select(pc_addr_select), .fetch(fetch));
  or or_6 (or_6_out, AND, ADD);
  assign DEST = or_7_out ? instruction[13:11] : 3'bz;  // Controlled_Buffer controlled_buffer_1
  or or_7 (or_7_out, ADDI, ANDI);
  assign DEST = LD ? instruction[12:10] : 3'bz;  // Controlled_Buffer controlled_buffer_2
  je_state je_state_1 (
    .address(instruction[9:0]), .alu_eq(EQ), .alu_ls(LS), .alu_gt(GT), .st___active(JE), .clock(clock),
    .reset(reset), .pc_enable(pc_enable), .pc_addr(pc_addr), .pc_addr_select(pc_addr_select), .fetch(fetch));
  // Probe on DEST
  assign DEST = or_6_out ? instruction[8:6] : 3'bz;  // Controlled_Buffer controlled_buffer_3
  assign SRC1 = or_8_out ? instruction[10:8] : 3'bz;  // Controlled_Buffer controlled_buffer_4
  or or_8 (or_8_out, ADDI, ANDI);
  assign SRC1 = ST ? instruction[12:10] : 3'bz;  // Controlled_Buffer controlled_buffer_5
  assign SRC1 = or_9_out ? instruction[5:3] : 3'bz;  // Controlled_Buffer controlled_buffer_6
  or or_9 (or_9_out, ADD, AND, CMP);
  Multiplexer #(.enable("false")) multiplexer_1 (.in0(1'b1), .in1(1'b0), .out(pc_addr_select), .sel(fetch));
  Multiplexer #(.enable("false")) multiplexer_2 (.in0(1'b0), .in1(1'b1), .out(pc_enable), .sel(fetch));
  cmp_state cmp_state_1 (
    .src1(SRC1), .reg_out1(reg_out_val1), .dest(DEST), .regz_out(regz_out), .src2(instruction[2:0]),
    .eq(alu_eq), .reg_out2(reg_out_val2), .ls(alu_ls), .gt(alu_gt), .alu_out(alu_out_value),
    .st___active(CMP), .clock(clock), .reset(reset), .regz_in(regz_in), .regz_enable(REGZ_ENABLE),
    .reg_out_addr1(reg_out_addr1), .reg_out_addr2(reg_out_addr2), .alu_in1(alu_in1), .alu_in_2(alu_in2),
    .alu_op(alu_op), .alu_enable(ALU_ENABLE5), .reg_in_add(reg_in_addr), .reg_in(reg_in_value),
    .reg_write(reg_write7), .fetch(fetch));
  jb_state jb_state_1 (
    .address(instruction[9:0]), .alu_eq(EQ), .alu_ls(LS), .alu_gt(GT), .st___active(JB), .clock(clock),
    .reset(reset), .pc_enable(pc_enable), .pc_addr(pc_addr), .pc_addr_select(pc_addr_select), .fetch(fetch));
  // Probe on SRC1
  or or_10 (reg_write, reg_write1, reg_write3, reg_write4, reg_write5, reg_write6);
  or or_11 (alu_enable, ALU_ENABLE2, ALU_ENABLE3, ALU_ENABLE5, ALU_ENABLE4, ALU_ENABLE1);
  jbe_state jbe_state_1 (
    .address(instruction[9:0]), .alu_eq(EQ), .alu_ls(LS), .alu_gt(GT), .st___active(JBE), .clock(clock),
    .reset(reset), .pc_enable(pc_enable), .pc_addr(pc_addr), .pc_addr_select(pc_addr_select), .fetch(fetch));

  // Other names for the same wires on the sheet: DESTI[2:0] = instruction[13:11]; SRCM[2:0] = instruction[12:10];
  //   SRCI[2:0] = instruction[10:8]; ADDRESS[9:0] = instruction[9:0]; ALU_OUT[15:0] = alu_out_value;
  //   DESTA1[2:0] = instruction[8:6]; IMM[7:0] = instruction[7:0]; RAM_IN[15:0] = ram_in_value;
  //   RAM_R_ENABLE = RAM_READ; RAM_W_ENABLE = RAM_WRITE; reg_in[15:0] = reg_in_value; reg_in_add[2:0] = reg_in_addr;
  //   reg_out1[15:0] = reg_out_val1; reg_out2[15:0] = reg_out_val2; reg_out_add1[2:0] = reg_out_addr1;
  //   reg_out_add2[2:0] = reg_out_addr2; reset_fsms = reset; SRC2[2:0] = instruction[2:0];
  //   SRCA1[2:0] = instruction[5:3]

  // Notes on the sheet:
  //   our special cpu regs
  //   those are our states
  //   this is our fetch instruction part
endmodule

module my_2x2_ram (
  input  [1:0] address_2bit,
  input  [15:0] data_input,
  input  enable_write,
  input  enable_read,
  input  reset,
  input  clock,
  output [15:0] data_output
);

  wire and_1_out, and_2_out, and_3_out, and_4_out, decoder_1_out0, decoder_1_out1, decoder_2_out0,
       decoder_2_out1;
  wire [15:0] flip_flop_store_1_output, flip_flop_store_2_output, flip_flop_store_3_output,
       flip_flop_store_4_output, multiplexer_1_out, multiplexer_2_out;

  Decoder #(.enable("false")) decoder_1 (.out0(decoder_1_out0), .out1(decoder_1_out1), .sel(address_2bit[1]));
  and and_1 (and_1_out, decoder_2_out0, enable_write, decoder_1_out0);
  and and_2 (and_2_out, decoder_2_out0, enable_write, decoder_1_out1);
  Decoder #(.enable("false")) decoder_2 (.out0(decoder_2_out0), .out1(decoder_2_out1), .sel(address_2bit[0]));
  flip_flop_store flip_flop_store_1 (
    .\input (data_input), .write_enable(and_1_out), .reset(reset), .clock(clock),
    .\output (flip_flop_store_1_output));
  flip_flop_store flip_flop_store_2 (
    .\input (data_input), .write_enable(and_2_out), .reset(reset), .clock(clock),
    .\output (flip_flop_store_2_output));
  and and_3 (and_3_out, decoder_2_out1, enable_write, decoder_1_out0);
  and and_4 (and_4_out, decoder_2_out1, enable_write, decoder_1_out1);
  flip_flop_store flip_flop_store_3 (
    .\input (data_input), .write_enable(and_3_out), .reset(reset), .clock(clock),
    .\output (flip_flop_store_3_output));
  flip_flop_store flip_flop_store_4 (
    .\input (data_input), .write_enable(and_4_out), .reset(reset), .clock(clock),
    .\output (flip_flop_store_4_output));
  Multiplexer #(.width(16)) multiplexer_1 (
    .in0(flip_flop_store_1_output), .in1(flip_flop_store_3_output), .out(multiplexer_1_out),
    .sel(address_2bit[0]), .en(enable_read));
  Multiplexer #(.width(16)) multiplexer_2 (
    .in0(flip_flop_store_2_output), .in1(flip_flop_store_4_output), .out(multiplexer_2_out),
    .sel(address_2bit[0]), .en(enable_read));
  Multiplexer #(.width(16)) multiplexer_3 (
    .in0(multiplexer_1_out), .in1(multiplexer_2_out), .out(data_output), .sel(address_2bit[1]),
    .en(enable_read));
endmodule

module _4x4_from_2x2 (
  input  [3:0] address_4bit,
  input  [15:0] data_input,
  input  enable_write,
  input  reset,
  input  clock,
  input  enable_read,
  output [15:0] data_output
);

  wire and_1_out, and_2_out, and_3_out, and_4_out, decoder_1_out0, decoder_1_out1, decoder_2_out0,
       decoder_2_out1;
  wire [15:0] multiplexer_1_out, multiplexer_2_out, my_2x2_ram_1_data_output, my_2x2_ram_2_data_output,
       my_2x2_ram_3_data_output, my_2x2_ram_4_data_output;

  Decoder #(.enable("false")) decoder_1 (.out0(decoder_1_out0), .out1(decoder_1_out1), .sel(address_4bit[3]));
  Decoder #(.enable("false")) decoder_2 (.out0(decoder_2_out0), .out1(decoder_2_out1), .sel(address_4bit[2]));
  and and_1 (and_1_out, decoder_2_out0, enable_write, decoder_1_out0);
  and and_2 (and_2_out, decoder_2_out0, enable_write, decoder_1_out1);
  my_2x2_ram my_2x2_ram_1 (
    .address_2bit(address_4bit[1:0]), .data_input(data_input), .enable_write(and_1_out),
    .enable_read(enable_read), .reset(reset), .clock(clock), .data_output(my_2x2_ram_1_data_output));
  my_2x2_ram my_2x2_ram_2 (
    .address_2bit(address_4bit[1:0]), .data_input(data_input), .enable_write(and_2_out),
    .enable_read(enable_read), .reset(reset), .clock(clock), .data_output(my_2x2_ram_2_data_output));
  and and_3 (and_3_out, decoder_2_out1, enable_write, decoder_1_out0);
  and and_4 (and_4_out, decoder_2_out1, enable_write, decoder_1_out1);
  my_2x2_ram my_2x2_ram_3 (
    .address_2bit(address_4bit[1:0]), .data_input(data_input), .enable_write(and_3_out),
    .enable_read(enable_read), .reset(reset), .clock(clock), .data_output(my_2x2_ram_3_data_output));
  my_2x2_ram my_2x2_ram_4 (
    .address_2bit(address_4bit[1:0]), .data_input(data_input), .enable_write(and_4_out),
    .enable_read(enable_read), .reset(reset), .clock(clock), .data_output(my_2x2_ram_4_data_output));
  Multiplexer #(.width(16)) multiplexer_1 (
    .in0(my_2x2_ram_2_data_output), .in1(my_2x2_ram_4_data_output), .out(multiplexer_1_out),
    .sel(address_4bit[2]), .en(enable_read));
  Multiplexer #(.width(16)) multiplexer_2 (
    .in0(my_2x2_ram_1_data_output), .in1(my_2x2_ram_3_data_output), .out(multiplexer_2_out),
    .sel(address_4bit[2]), .en(enable_read));
  Multiplexer #(.width(16)) multiplexer_3 (
    .in0(multiplexer_2_out), .in1(multiplexer_1_out), .out(data_output), .sel(address_4bit[3]),
    .en(enable_read));
endmodule

module _6x6_from_4x4 (
  input  [5:0] address_6bit,
  input  [15:0] data_input,
  input  enable_write,
  input  reset,
  input  clock,
  input  enable_read,
  output [15:0] data_output
);

  wire and_1_out, and_2_out, and_3_out, and_4_out, decoder_1_out0, decoder_1_out1, decoder_2_out0,
       decoder_2_out1;
  wire [15:0] multiplexer_1_out, multiplexer_2_out, n4x4_from_2x2_1_data_output, n4x4_from_2x2_2_data_output,
       n4x4_from_2x2_3_data_output, n4x4_from_2x2_4_data_output;

  Decoder #(.enable("false")) decoder_1 (.out0(decoder_1_out0), .out1(decoder_1_out1), .sel(address_6bit[5]));
  and and_1 (and_1_out, decoder_2_out0, enable_write, decoder_1_out0);
  and and_2 (and_2_out, decoder_2_out0, enable_write, decoder_1_out1);
  Decoder #(.enable("false")) decoder_2 (.out0(decoder_2_out0), .out1(decoder_2_out1), .sel(address_6bit[4]));
  _4x4_from_2x2 u_4x4_from_2x2_1 (
    .address_4bit(address_6bit[3:0]), .data_input(data_input), .enable_write(and_1_out), .reset(reset),
    .clock(clock), .enable_read(enable_read), .data_output(n4x4_from_2x2_1_data_output));
  _4x4_from_2x2 u_4x4_from_2x2_2 (
    .address_4bit(address_6bit[3:0]), .data_input(data_input), .enable_write(and_2_out), .reset(reset),
    .clock(clock), .enable_read(enable_read), .data_output(n4x4_from_2x2_2_data_output));
  _4x4_from_2x2 u_4x4_from_2x2_3 (
    .address_4bit(address_6bit[3:0]), .data_input(data_input), .enable_write(and_3_out), .reset(reset),
    .clock(clock), .enable_read(enable_read), .data_output(n4x4_from_2x2_3_data_output));
  and and_3 (and_3_out, decoder_2_out1, enable_write, decoder_1_out0);
  and and_4 (and_4_out, decoder_2_out1, enable_write, decoder_1_out1);
  _4x4_from_2x2 u_4x4_from_2x2_4 (
    .address_4bit(address_6bit[3:0]), .data_input(data_input), .enable_write(and_4_out), .reset(reset),
    .clock(clock), .enable_read(enable_read), .data_output(n4x4_from_2x2_4_data_output));
  Multiplexer #(.width(16)) multiplexer_1 (
    .in0(n4x4_from_2x2_1_data_output), .in1(n4x4_from_2x2_3_data_output), .out(multiplexer_1_out),
    .sel(address_6bit[4]), .en(enable_read));
  Multiplexer #(.width(16)) multiplexer_2 (
    .in0(n4x4_from_2x2_2_data_output), .in1(n4x4_from_2x2_4_data_output), .out(multiplexer_2_out),
    .sel(address_6bit[4]), .en(enable_read));
  Multiplexer #(.width(16)) multiplexer_3 (
    .in0(multiplexer_1_out), .in1(multiplexer_2_out), .out(data_output), .sel(address_6bit[5]),
    .en(enable_read));
endmodule

module _8x8_from_6x6 (
  input  [7:0] address_8bit,
  input  [15:0] data_input,
  input  enable_write,
  input  reset,
  input  clock,
  input  enable_read,
  output [15:0] data_output
);

  wire and_1_out, and_2_out, and_3_out, and_4_out, decoder_1_out0, decoder_1_out1, decoder_2_out0,
       decoder_2_out1;
  wire [15:0] multiplexer_1_out, multiplexer_2_out, n6x6_from_4x4_1_data_output, n6x6_from_4x4_2_data_output,
       n6x6_from_4x4_3_data_output, n6x6_from_4x4_4_data_output;

  Decoder #(.enable("false")) decoder_1 (.out0(decoder_1_out0), .out1(decoder_1_out1), .sel(address_8bit[7]));
  and and_1 (and_1_out, decoder_2_out0, enable_write, decoder_1_out0);
  and and_2 (and_2_out, decoder_2_out0, enable_write, decoder_1_out1);
  Decoder #(.enable("false")) decoder_2 (.out0(decoder_2_out0), .out1(decoder_2_out1), .sel(address_8bit[6]));
  _6x6_from_4x4 u_6x6_from_4x4_1 (
    .address_6bit(address_8bit[5:0]), .data_input(data_input), .enable_write(and_1_out), .reset(reset),
    .clock(clock), .enable_read(enable_read), .data_output(n6x6_from_4x4_1_data_output));
  _6x6_from_4x4 u_6x6_from_4x4_2 (
    .address_6bit(address_8bit[5:0]), .data_input(data_input), .enable_write(and_2_out), .reset(reset),
    .clock(clock), .enable_read(enable_read), .data_output(n6x6_from_4x4_2_data_output));
  _6x6_from_4x4 u_6x6_from_4x4_3 (
    .address_6bit(address_8bit[5:0]), .data_input(data_input), .enable_write(and_3_out), .reset(reset),
    .clock(clock), .enable_read(enable_read), .data_output(n6x6_from_4x4_3_data_output));
  and and_3 (and_3_out, decoder_2_out1, enable_write, decoder_1_out0);
  and and_4 (and_4_out, decoder_2_out1, enable_write, decoder_1_out1);
  _6x6_from_4x4 u_6x6_from_4x4_4 (
    .address_6bit(address_8bit[5:0]), .data_input(data_input), .enable_write(and_4_out), .reset(reset),
    .clock(clock), .enable_read(enable_read), .data_output(n6x6_from_4x4_4_data_output));
  Multiplexer #(.width(16)) multiplexer_1 (
    .in0(n6x6_from_4x4_1_data_output), .in1(n6x6_from_4x4_3_data_output), .out(multiplexer_1_out),
    .sel(address_8bit[6]), .en(enable_read));
  Multiplexer #(.width(16)) multiplexer_2 (
    .in0(n6x6_from_4x4_2_data_output), .in1(n6x6_from_4x4_4_data_output), .out(multiplexer_2_out),
    .sel(address_8bit[6]), .en(enable_read));
  Multiplexer #(.width(16)) multiplexer_3 (
    .in0(multiplexer_1_out), .in1(multiplexer_2_out), .out(data_output), .sel(address_8bit[7]),
    .en(enable_read));
endmodule

module _10x10_from_8x8 (
  input  [9:0] address_10bit,
  input  [15:0] data_input,
  input  enable_write,
  input  reset,
  input  clock,
  input  enable_read,
  output [15:0] data_output
);

  wire and_1_out, and_2_out, and_3_out, and_4_out, decoder_1_out0, decoder_1_out1, decoder_2_out0,
       decoder_2_out1;
  wire [15:0] multiplexer_1_out, multiplexer_2_out, n8x8_from_6x6_1_data_output, n8x8_from_6x6_2_data_output,
       n8x8_from_6x6_3_data_output, n8x8_from_6x6_4_data_output;

  Decoder #(.enable("false")) decoder_1 (.out0(decoder_1_out0), .out1(decoder_1_out1), .sel(address_10bit[9]));
  and and_1 (and_1_out, decoder_2_out0, enable_write, decoder_1_out0);
  and and_2 (and_2_out, decoder_2_out0, enable_write, decoder_1_out1);
  Decoder #(.enable("false")) decoder_2 (.out0(decoder_2_out0), .out1(decoder_2_out1), .sel(address_10bit[8]));
  _8x8_from_6x6 u_8x8_from_6x6_1 (
    .address_8bit(address_10bit[7:0]), .data_input(data_input), .enable_write(and_1_out), .reset(reset),
    .clock(clock), .enable_read(enable_read), .data_output(n8x8_from_6x6_1_data_output));
  _8x8_from_6x6 u_8x8_from_6x6_2 (
    .address_8bit(address_10bit[7:0]), .data_input(data_input), .enable_write(and_2_out), .reset(reset),
    .clock(clock), .enable_read(enable_read), .data_output(n8x8_from_6x6_2_data_output));
  and and_3 (and_3_out, decoder_2_out1, enable_write, decoder_1_out0);
  and and_4 (and_4_out, decoder_2_out1, enable_write, decoder_1_out1);
  _8x8_from_6x6 u_8x8_from_6x6_3 (
    .address_8bit(address_10bit[7:0]), .data_input(data_input), .enable_write(and_3_out), .reset(reset),
    .clock(clock), .enable_read(enable_read), .data_output(n8x8_from_6x6_3_data_output));
  _8x8_from_6x6 u_8x8_from_6x6_4 (
    .address_8bit(address_10bit[7:0]), .data_input(data_input), .enable_write(and_4_out), .reset(reset),
    .clock(clock), .enable_read(enable_read), .data_output(n8x8_from_6x6_4_data_output));
  Multiplexer #(.width(16)) multiplexer_1 (
    .in0(n8x8_from_6x6_1_data_output), .in1(n8x8_from_6x6_3_data_output), .out(multiplexer_1_out),
    .sel(address_10bit[8]), .en(enable_read));
  Multiplexer #(.width(16)) multiplexer_2 (
    .in0(n8x8_from_6x6_2_data_output), .in1(n8x8_from_6x6_4_data_output), .out(multiplexer_2_out),
    .sel(address_10bit[8]), .en(enable_read));
  Multiplexer #(.width(16)) multiplexer_3 (
    .in0(multiplexer_1_out), .in1(multiplexer_2_out), .out(data_output), .sel(address_10bit[9]),
    .en(enable_read));
endmodule

module add (
  input  a,
  input  b,
  input  carry,
  output CarryOut,
  output Sum
);

  wire and_1_out, and_2_out, and_3_out, and_4_out, and_5_out, and_6_out, and_7_out, not_1_out, not_2_out,
       not_3_out, not_4_out, not_5_out, not_6_out, not_7_out, not_8_out;

  not not_1 (not_1_out, b);
  not not_2 (not_2_out, a);
  not not_3 (not_3_out, b);
  not not_4 (not_4_out, carry);
  not not_5 (not_5_out, a);
  not not_6 (not_6_out, carry);
  not not_7 (not_7_out, a);
  not not_8 (not_8_out, b);
  and and_1 (and_1_out, a, not_1_out, carry);
  and and_2 (and_2_out, not_2_out, b, carry);
  and and_3 (and_3_out, a, b);
  and and_4 (and_4_out, a, not_3_out, not_4_out);
  and and_5 (and_5_out, not_5_out, b, not_6_out);
  and and_6 (and_6_out, not_7_out, not_8_out, carry);
  and and_7 (and_7_out, a, b, carry);
  or or_1 (CarryOut, and_1_out, and_2_out, and_3_out);
  or or_2 (Sum, and_4_out, and_5_out, and_6_out, and_7_out);
endmodule

module half_adder (
  input  a,
  input  b,
  output sum,
  output c_out
);

  xor xor_1 (sum, a, b);
  and and_1 (c_out, a, b);
endmodule

module comparator (
  input  [15:0] a,
  input  [15:0] b,
  output gt,
  output lt,
  output eq
);

  wire compare_1_eq_out, compare_1_gt_out, compare_1_lt_out, compare_2_eq_out, compare_2_gt_out,
       compare_2_lt_out, compare_3_eq_out, compare_3_gt_out, compare_3_lt_out, compare_4_eq_out,
       compare_4_gt_out, compare_4_lt_out, compare_5_eq_out, compare_5_gt_out, compare_5_lt_out,
       compare_6_eq_out, compare_6_gt_out, compare_6_lt_out, compare_7_eq_out, compare_7_gt_out,
       compare_7_lt_out, compare_8_eq_out, compare_8_gt_out, compare_8_lt_out, compare_9_eq_out,
       compare_9_gt_out, compare_9_lt_out, compare_10_eq_out, compare_10_gt_out, compare_10_lt_out,
       compare_11_eq_out, compare_11_gt_out, compare_11_lt_out, compare_12_eq_out, compare_12_gt_out,
       compare_12_lt_out, compare_13_eq_out, compare_13_gt_out, compare_13_lt_out, compare_14_eq_out,
       compare_14_gt_out, compare_14_lt_out, half_compare_1_eq, half_compare_1_gt, half_compare_1_lt;

  half_compare half_compare_1 (
    .a(a[15]), .b(b[15]), .gt(half_compare_1_gt), .lt(half_compare_1_lt), .eq(half_compare_1_eq));  // open: reverse
  compare compare_1 (
    .a(a[14]), .b(b[14]), .gt_in(half_compare_1_gt), .lt_in(half_compare_1_lt), .eq_in(half_compare_1_eq),
    .gt_out(compare_1_gt_out), .lt_out(compare_1_lt_out), .eq_out(compare_1_eq_out));
  compare compare_2 (
    .a(a[13]), .b(b[13]), .gt_in(compare_1_gt_out), .lt_in(compare_1_lt_out), .eq_in(compare_1_eq_out),
    .gt_out(compare_2_gt_out), .lt_out(compare_2_lt_out), .eq_out(compare_2_eq_out));
  compare compare_3 (
    .a(a[11]), .b(b[11]), .gt_in(compare_4_gt_out), .lt_in(compare_4_lt_out), .eq_in(compare_4_eq_out),
    .gt_out(compare_3_gt_out), .lt_out(compare_3_lt_out), .eq_out(compare_3_eq_out));
  compare compare_4 (
    .a(a[12]), .b(b[12]), .gt_in(compare_2_gt_out), .lt_in(compare_2_lt_out), .eq_in(compare_2_eq_out),
    .gt_out(compare_4_gt_out), .lt_out(compare_4_lt_out), .eq_out(compare_4_eq_out));
  compare compare_5 (
    .a(a[10]), .b(b[10]), .gt_in(compare_3_gt_out), .lt_in(compare_3_lt_out), .eq_in(compare_3_eq_out),
    .gt_out(compare_5_gt_out), .lt_out(compare_5_lt_out), .eq_out(compare_5_eq_out));
  compare compare_6 (
    .a(a[9]), .b(b[9]), .gt_in(compare_5_gt_out), .lt_in(compare_5_lt_out), .eq_in(compare_5_eq_out),
    .gt_out(compare_6_gt_out), .lt_out(compare_6_lt_out), .eq_out(compare_6_eq_out));
  compare compare_7 (
    .a(a[7]), .b(b[7]), .gt_in(compare_8_gt_out), .lt_in(compare_8_lt_out), .eq_in(compare_8_eq_out),
    .gt_out(compare_7_gt_out), .lt_out(compare_7_lt_out), .eq_out(compare_7_eq_out));
  compare compare_8 (
    .a(a[8]), .b(b[8]), .gt_in(compare_6_gt_out), .lt_in(compare_6_lt_out), .eq_in(compare_6_eq_out),
    .gt_out(compare_8_gt_out), .lt_out(compare_8_lt_out), .eq_out(compare_8_eq_out));
  compare compare_9 (
    .a(a[6]), .b(b[6]), .gt_in(compare_7_gt_out), .lt_in(compare_7_lt_out), .eq_in(compare_7_eq_out),
    .gt_out(compare_9_gt_out), .lt_out(compare_9_lt_out), .eq_out(compare_9_eq_out));
  compare compare_10 (
    .a(a[5]), .b(b[5]), .gt_in(compare_9_gt_out), .lt_in(compare_9_lt_out), .eq_in(compare_9_eq_out),
    .gt_out(compare_10_gt_out), .lt_out(compare_10_lt_out), .eq_out(compare_10_eq_out));
  compare compare_11 (
    .a(a[3]), .b(b[3]), .gt_in(compare_12_gt_out), .lt_in(compare_12_lt_out), .eq_in(compare_12_eq_out),
    .gt_out(compare_11_gt_out), .lt_out(compare_11_lt_out), .eq_out(compare_11_eq_out));
  compare compare_12 (
    .a(a[4]), .b(b[4]), .gt_in(compare_10_gt_out), .lt_in(compare_10_lt_out), .eq_in(compare_10_eq_out),
    .gt_out(compare_12_gt_out), .lt_out(compare_12_lt_out), .eq_out(compare_12_eq_out));
  compare compare_13 (
    .a(a[2]), .b(b[2]), .gt_in(compare_11_gt_out), .lt_in(compare_11_lt_out), .eq_in(compare_11_eq_out),
    .gt_out(compare_13_gt_out), .lt_out(compare_13_lt_out), .eq_out(compare_13_eq_out));
  compare compare_14 (
    .a(a[1]), .b(b[1]), .gt_in(compare_13_gt_out), .lt_in(compare_13_lt_out), .eq_in(compare_13_eq_out),
    .gt_out(compare_14_gt_out), .lt_out(compare_14_lt_out), .eq_out(compare_14_eq_out));
  compare compare_15 (
    .a(a[0]), .b(b[0]), .gt_in(compare_14_gt_out), .lt_in(compare_14_lt_out), .eq_in(compare_14_eq_out),
    .gt_out(gt), .lt_out(lt), .eq_out(eq));
endmodule

module adder (
  input  [15:0] a,
  input  [15:0] b,
  output [15:0] sum,
  output overflow,
  output isWrong
);

  wire add_1_carryout, add_2_carryout, add_3_carryout, add_4_carryout, add_5_carryout, add_6_carryout,
       add_7_carryout, add_8_carryout, add_9_carryout, add_10_carryout, add_11_carryout, add_12_carryout,
       add_13_carryout, add_14_carryout, half_adder_1_c_out;

  half_adder half_adder_1 (.a(a[0]), .b(b[0]), .sum(sum[0]), .c_out(half_adder_1_c_out));
  add add_1 (.a(half_adder_1_c_out), .b(a[1]), .carry(b[1]), .CarryOut(add_1_carryout), .Sum(sum[1]));
  add add_2 (.a(add_1_carryout), .b(a[2]), .carry(b[2]), .CarryOut(add_2_carryout), .Sum(sum[2]));
  add add_3 (.a(add_2_carryout), .b(a[3]), .carry(b[3]), .CarryOut(add_3_carryout), .Sum(sum[3]));
  add add_4 (.a(add_3_carryout), .b(a[4]), .carry(b[4]), .CarryOut(add_4_carryout), .Sum(sum[4]));
  add add_5 (.a(add_4_carryout), .b(a[5]), .carry(b[5]), .CarryOut(add_5_carryout), .Sum(sum[5]));
  add add_6 (.a(add_5_carryout), .b(a[6]), .carry(b[6]), .CarryOut(add_6_carryout), .Sum(sum[6]));
  add add_7 (.a(add_6_carryout), .b(a[7]), .carry(b[7]), .CarryOut(add_7_carryout), .Sum(sum[7]));
  add add_8 (.a(add_7_carryout), .b(a[8]), .carry(b[8]), .CarryOut(add_8_carryout), .Sum(sum[8]));
  add add_9 (.a(add_8_carryout), .b(a[9]), .carry(b[9]), .CarryOut(add_9_carryout), .Sum(sum[9]));
  add add_10 (.a(add_9_carryout), .b(a[10]), .carry(b[10]), .CarryOut(add_10_carryout), .Sum(sum[10]));
  add add_11 (.a(add_10_carryout), .b(a[11]), .carry(b[11]), .CarryOut(add_11_carryout), .Sum(sum[11]));
  add add_12 (.a(add_11_carryout), .b(a[12]), .carry(b[12]), .CarryOut(add_12_carryout), .Sum(sum[12]));
  add add_13 (.a(add_12_carryout), .b(a[13]), .carry(b[13]), .CarryOut(add_13_carryout), .Sum(sum[13]));
  add add_14 (.a(add_13_carryout), .b(a[14]), .carry(b[14]), .CarryOut(add_14_carryout), .Sum(sum[14]));
  add add_15 (.a(add_14_carryout), .b(a[15]), .carry(b[15]), .CarryOut(overflow), .Sum(sum[15]));
  xor xor_1 (isWrong, overflow, add_14_carryout);
endmodule

module half_compare (
  input  a,
  input  b,
  output gt,
  output lt,
  output eq,
  output reverse
);

  wire not_1_out, not_2_out;

  not not_1 (not_1_out, a);
  not not_2 (not_2_out, b);
  and and_1 (gt, not_1_out, b);
  and and_2 (lt, a, not_2_out);
  xnor xnor_1 (eq, a, b);
  and and_3 (reverse, a, b);
endmodule

module compare (
  input  a,
  input  b,
  input  gt_in,
  input  lt_in,
  input  eq_in,
  output gt_out,
  output lt_out,
  output eq_out
);

  wire and_1_out, and_2_out, not_1_out, not_2_out, xnor_1_out;

  not not_1 (not_1_out, b);
  and and_1 (and_1_out, a, not_1_out, eq_in);
  not not_2 (not_2_out, a);
  or or_1 (gt_out, and_1_out, gt_in);
  and and_2 (and_2_out, not_2_out, b, eq_in);
  or or_2 (lt_out, and_2_out, lt_in);
  xnor xnor_1 (xnor_1_out, a, b);
  and and_3 (eq_out, xnor_1_out, eq_in);
endmodule

// ST
module st_state (
  input  [2:0] src1,
  input  [15:0] reg_out1,
  input  [15:0] regz_out,
  input  [9:0] ADDRESS,
  input  LD___active,
  input  clock,
  input  reset,
  output [2:0] reg_out_add1,
  output [15:0] regz_in,
  output regz_enable,
  output [15:0] ram_in,
  output [9:0] RAM_ADDR,
  output RAM_W_ENABLE,
  output pc_enable,
  output pc_addr_select,
  output fetch_next_inst
);

  wire and_1_out, decoder_1_out0, decoder_1_out1, decoder_1_out2, decoder_1_out3, not_1_out, or_1_out;
  wire [1:0] adder_1_out, register_1_q;

  and and_1 (and_1_out, LD___active, clock);
  // Probe on register_1_q
  Decoder #(.select(2), .enable("false")) decoder_1 (
    .out0(decoder_1_out0), .out1(decoder_1_out1), .out2(decoder_1_out2), .out3(decoder_1_out3),
    .sel(register_1_q));
  not not_1 (not_1_out, LD___active);
  // Probe on reg_out1
  Adder #(.width(2)) adder_1 (.a(register_1_q), .b(2'b01), .out(adder_1_out));  // open: cin, cout
  // Probe on src1
  Register #(.width(2)) register_1 (.D(adder_1_out), .Q(register_1_q), .clk(and_1_out), .clr(or_1_out));  // open: en
  or or_1 (or_1_out, not_1_out, reset);
  assign reg_out_add1 = decoder_1_out1 ? src1 : 3'bz;  // Controlled_Buffer controlled_buffer_1
  assign regz_in = decoder_1_out1 ? reg_out1 : 16'bz;  // Controlled_Buffer controlled_buffer_2
  assign regz_enable = decoder_1_out1 ? 1'b1 : 1'bz;  // Controlled_Buffer controlled_buffer_3
  // Probe on regz_out
  assign ram_in = decoder_1_out2 ? regz_out : 16'bz;  // Controlled_Buffer controlled_buffer_4
  assign RAM_ADDR = decoder_1_out2 ? ADDRESS : 10'bz;  // Controlled_Buffer controlled_buffer_5
  Multiplexer #(.enable("false")) multiplexer_1 (.in0(1'b0), .in1(1'b1), .out(RAM_W_ENABLE), .sel(decoder_1_out2));
  assign fetch_next_inst = decoder_1_out3 ? 1'b1 : 1'bz;  // Controlled_Buffer controlled_buffer_6

  // Other names for the same wires on the sheet: fetch = fetch_next_inst
endmodule

// LD
module ld_state (
  input  [2:0] dest,
  input  [15:0] regz_out,
  input  [15:0] ram_out,
  input  [9:0] addr,
  input  st___active,
  input  clock,
  input  reset,
  output [2:0] reg_in_addr,
  output [15:0] reg_in,
  output regz_en,
  output [9:0] ram_addr,
  output ram_r_ena,
  output [15:0] regz_in,
  output reg_write,
  output fetch
);

  wire and_1_out, decoder_1_out0, decoder_1_out1, decoder_1_out2, decoder_1_out3, not_1_out, or_1_out;
  wire [1:0] adder_1_out, register_1_q;

  and and_1 (and_1_out, st___active, clock);
  // Probe on register_1_q
  Decoder #(.select(2)) decoder_1 (
    .out0(decoder_1_out0), .out1(decoder_1_out1), .out2(decoder_1_out2), .out3(decoder_1_out3),
    .sel(register_1_q));  // open: en
  not not_1 (not_1_out, st___active);
  Adder #(.width(2)) adder_1 (.a(register_1_q), .b(2'b01), .out(adder_1_out));  // open: cin, cout
  Register #(.width(2)) register_1 (.D(adder_1_out), .Q(register_1_q), .clk(and_1_out), .clr(or_1_out));  // open: en
  or or_1 (or_1_out, not_1_out, reset);
  assign ram_addr = decoder_1_out1 ? addr : 10'bz;  // Controlled_Buffer controlled_buffer_1
  Multiplexer #(.enable("false")) multiplexer_1 (.in0(1'b0), .in1(1'b1), .out(ram_r_ena), .sel(decoder_1_out1));
  assign regz_en = decoder_1_out1 ? 1'b1 : 1'bz;  // Controlled_Buffer controlled_buffer_2
  assign regz_in = decoder_1_out1 ? ram_out : 16'bz;  // Controlled_Buffer controlled_buffer_3
  // Probe on regz_out
  assign reg_in_addr = decoder_1_out2 ? dest : 3'bz;  // Controlled_Buffer controlled_buffer_4
  // Probe on reg_in
  assign reg_in = decoder_1_out2 ? regz_out : 16'bz;  // Controlled_Buffer controlled_buffer_5
  Multiplexer #(.enable("false")) multiplexer_2 (.in0(1'b0), .in1(1'b1), .out(reg_write), .sel(decoder_1_out2));
  assign fetch = decoder_1_out3 ? 1'b1 : 1'bz;  // Controlled_Buffer controlled_buffer_6

  // Other names for the same wires on the sheet: ADDRESS[9:0] = addr; RAM_R_ENABLE = ram_r_ena;
  //   reg_in_add[2:0] = reg_in_addr; REGZ_ENABLE = regz_en
endmodule

// ADDI
module addi_state (
  input  [2:0] src1,
  input  [15:0] reg_out1,
  input  [15:0] regz_out,
  input  [2:0] dest,
  input  eq,
  input  [7:0] imm,
  input  ls,
  input  gt,
  input  [15:0] alu_out,
  input  st___active,
  input  clock,
  input  reset,
  output [15:0] regz_in,
  output regz_enable,
  output [2:0] reg_out_addr1,
  output [15:0] alu_in1,
  output [15:0] alu_in_2,
  output alu_op,
  output alu_enable,
  output [2:0] reg_in_add,
  output [15:0] reg_in,
  output reg_write,
  output fetch
);

  wire and_1_out, decoder_1_out0, decoder_1_out1, decoder_1_out2, decoder_1_out3, not_1_out, or_1_out;
  wire [1:0] adder_1_out, register_1_q;

  and and_1 (and_1_out, st___active, clock);
  // Probe on register_1_q
  Decoder #(.select(2), .enable("false")) decoder_1 (
    .out0(decoder_1_out0), .out1(decoder_1_out1), .out2(decoder_1_out2), .out3(decoder_1_out3),
    .sel(register_1_q));
  not not_1 (not_1_out, st___active);
  // Probe on alu_out
  Adder #(.width(2)) adder_1 (.a(register_1_q), .b(2'b01), .out(adder_1_out));  // open: cin, cout
  // Probe on {{8{1'b0}}, imm}
  Register #(.width(2)) register_1 (.D(adder_1_out), .Q(register_1_q), .clk(and_1_out), .clr(or_1_out));  // open: en
  or or_1 (or_1_out, not_1_out, reset);
  assign reg_out_addr1 = decoder_1_out1 ? src1 : 3'bz;  // Controlled_Buffer controlled_buffer_1
  // Probe on alu_in1
  assign alu_in1 = decoder_1_out1 ? reg_out1 : 16'bz;  // Controlled_Buffer controlled_buffer_2
  assign alu_in_2 = decoder_1_out1 ? {{8{1'b0}}, imm} : 16'bz;  // Controlled_Buffer controlled_buffer_3
  assign alu_op = decoder_1_out1 ? 1'b1 : 1'bz;  // Controlled_Buffer controlled_buffer_4
  Multiplexer #(.enable("false")) multiplexer_1 (.in0(1'b0), .in1(1'b1), .out(alu_enable), .sel(decoder_1_out1));
  assign regz_in = decoder_1_out1 ? alu_out : 16'bz;  // Controlled_Buffer controlled_buffer_5
  assign regz_enable = decoder_1_out1 ? 1'b1 : 1'bz;  // Controlled_Buffer controlled_buffer_6
  // Probe on regz_out
  assign reg_in_add = decoder_1_out2 ? dest : 3'bz;  // Controlled_Buffer controlled_buffer_7
  assign reg_in = decoder_1_out2 ? regz_out : 16'bz;  // Controlled_Buffer controlled_buffer_8
  Multiplexer #(.enable("false")) multiplexer_2 (.in0(1'b0), .in1(1'b1), .out(reg_write), .sel(decoder_1_out2));
  assign fetch = decoder_1_out3 ? 1'b1 : 1'bz;  // Controlled_Buffer controlled_buffer_9

  // Other names for the same wires on the sheet: ALU_IN2[15:0] = alu_in_2; reg_out_add1[2:0] = reg_out_addr1
endmodule

// ANDI
module andi_state (
  input  [2:0] src1,
  input  [15:0] reg_out1,
  input  [15:0] regz_out,
  input  [2:0] dest,
  input  eq,
  input  [7:0] imm,
  input  ls,
  input  gt,
  input  [15:0] alu_out,
  input  st___active,
  input  clock,
  input  reset,
  output [15:0] regz_in,
  output regz_enable,
  output [2:0] reg_out_addr1,
  output [15:0] alu_in1,
  output [15:0] alu_in_2,
  output alu_op,
  output alu_enable,
  output [2:0] reg_in_add,
  output [15:0] reg_in,
  output reg_write,
  output fetch
);

  wire and_1_out, decoder_1_out0, decoder_1_out1, decoder_1_out2, decoder_1_out3, not_1_out, or_1_out;
  wire [1:0] adder_1_out, register_1_q;

  and and_1 (and_1_out, st___active, clock);
  // Probe on register_1_q
  Decoder #(.select(2), .enable("false")) decoder_1 (
    .out0(decoder_1_out0), .out1(decoder_1_out1), .out2(decoder_1_out2), .out3(decoder_1_out3),
    .sel(register_1_q));
  not not_1 (not_1_out, st___active);
  Adder #(.width(2)) adder_1 (.a(register_1_q), .b(2'b01), .out(adder_1_out));  // open: cin, cout
  // Probe on {{8{1'b0}}, imm}
  Register #(.width(2)) register_1 (.D(adder_1_out), .Q(register_1_q), .clk(and_1_out), .clr(or_1_out));  // open: en
  or or_1 (or_1_out, not_1_out, reset);
  assign reg_out_addr1 = decoder_1_out1 ? src1 : 3'bz;  // Controlled_Buffer controlled_buffer_1
  assign alu_in1 = decoder_1_out1 ? reg_out1 : 16'bz;  // Controlled_Buffer controlled_buffer_2
  assign alu_in_2 = decoder_1_out1 ? {{8{1'b0}}, imm} : 16'bz;  // Controlled_Buffer controlled_buffer_3
  assign alu_op = decoder_1_out1 ? 1'b0 : 1'bz;  // Controlled_Buffer controlled_buffer_4
  Multiplexer #(.enable("false")) multiplexer_1 (.in0(1'b0), .in1(1'b1), .out(alu_enable), .sel(decoder_1_out1));
  assign regz_in = decoder_1_out1 ? alu_out : 16'bz;  // Controlled_Buffer controlled_buffer_5
  assign regz_enable = decoder_1_out1 ? 1'b1 : 1'bz;  // Controlled_Buffer controlled_buffer_6
  // Probe on regz_out
  assign reg_in_add = decoder_1_out2 ? dest : 3'bz;  // Controlled_Buffer controlled_buffer_7
  assign reg_in = decoder_1_out2 ? regz_out : 16'bz;  // Controlled_Buffer controlled_buffer_8
  Multiplexer #(.enable("false")) multiplexer_2 (.in0(1'b0), .in1(1'b1), .out(reg_write), .sel(decoder_1_out2));
  assign fetch = decoder_1_out3 ? 1'b1 : 1'bz;  // Controlled_Buffer controlled_buffer_9

  // Other names for the same wires on the sheet: ALU_IN2[15:0] = alu_in_2; reg_out_add1[2:0] = reg_out_addr1
endmodule

// ADD
module add_state (
  input  [2:0] src1,
  input  [15:0] reg_out1,
  input  [2:0] dest,
  input  [15:0] regz_out,
  input  [2:0] src2,
  input  eq,
  input  [15:0] reg_out2,
  input  ls,
  input  gt,
  input  [15:0] alu_out,
  input  st___active,
  input  clock,
  input  reset,
  output [15:0] regz_in,
  output regz_enable,
  output [2:0] reg_out_addr1,
  output [2:0] reg_out_addr2,
  output [15:0] alu_in1,
  output [15:0] alu_in_2,
  output alu_op,
  output alu_enable,
  output [2:0] reg_in_add,
  output [15:0] reg_in,
  output reg_write,
  output fetch
);

  wire and_1_out, decoder_1_out0, decoder_1_out1, decoder_1_out2, decoder_1_out3, not_1_out, or_1_out;
  wire [1:0] adder_1_out, register_1_q;

  and and_1 (and_1_out, st___active, clock);
  // Probe on register_1_q
  Decoder #(.select(2), .enable("false")) decoder_1 (
    .out0(decoder_1_out0), .out1(decoder_1_out1), .out2(decoder_1_out2), .out3(decoder_1_out3),
    .sel(register_1_q));
  not not_1 (not_1_out, st___active);
  // Probe on alu_out
  Adder #(.width(2)) adder_1 (.a(register_1_q), .b(2'b01), .out(adder_1_out));  // open: cin, cout
  // Probe on reg_out2
  Register #(.width(2)) register_1 (.D(adder_1_out), .Q(register_1_q), .clk(and_1_out), .clr(or_1_out));  // open: en
  or or_1 (or_1_out, not_1_out, reset);
  assign reg_out_addr1 = decoder_1_out1 ? src1 : 3'bz;  // Controlled_Buffer controlled_buffer_1
  assign alu_in1 = decoder_1_out1 ? reg_out1 : 16'bz;  // Controlled_Buffer controlled_buffer_2
  assign reg_out_addr2 = decoder_1_out1 ? src2 : 3'bz;  // Controlled_Buffer controlled_buffer_3
  assign alu_in_2 = decoder_1_out1 ? reg_out2 : 16'bz;  // Controlled_Buffer controlled_buffer_4
  assign alu_op = decoder_1_out1 ? 1'b1 : 1'bz;  // Controlled_Buffer controlled_buffer_5
  Multiplexer #(.enable("false")) multiplexer_1 (.in0(1'b0), .in1(1'b1), .out(alu_enable), .sel(decoder_1_out1));
  assign regz_in = decoder_1_out1 ? alu_out : 16'bz;  // Controlled_Buffer controlled_buffer_6
  assign regz_enable = decoder_1_out1 ? 1'b1 : 1'bz;  // Controlled_Buffer controlled_buffer_7
  // Probe on regz_out
  assign reg_in_add = decoder_1_out2 ? dest : 3'bz;  // Controlled_Buffer controlled_buffer_8
  assign reg_in = decoder_1_out2 ? regz_out : 16'bz;  // Controlled_Buffer controlled_buffer_9
  Multiplexer #(.enable("false")) multiplexer_2 (.in0(1'b0), .in1(1'b1), .out(reg_write), .sel(decoder_1_out2));
  assign fetch = decoder_1_out3 ? 1'b1 : 1'bz;  // Controlled_Buffer controlled_buffer_10

  // Other names for the same wires on the sheet: ALU_IN2[15:0] = alu_in_2; reg_out_add1[2:0] = reg_out_addr1;
  //   reg_out_add2[2:0] = reg_out_addr2
endmodule

// AND
module and_state (
  input  [2:0] src1,
  input  [15:0] reg_out1,
  input  [2:0] dest,
  input  [15:0] regz_out,
  input  [2:0] src2,
  input  eq,
  input  [15:0] reg_out2,
  input  ls,
  input  gt,
  input  [15:0] alu_out,
  input  st___active,
  input  clock,
  input  reset,
  output [15:0] regz_in,
  output regz_enable,
  output [2:0] reg_out_addr1,
  output [2:0] reg_out_addr2,
  output [15:0] alu_in1,
  output [15:0] alu_in_2,
  output alu_op,
  output alu_enable,
  output [2:0] reg_in_add,
  output [15:0] reg_in,
  output reg_write,
  output fetch
);

  wire and_1_out, decoder_1_out0, decoder_1_out1, decoder_1_out2, decoder_1_out3, not_1_out, or_1_out;
  wire [1:0] adder_1_out, register_1_q;

  and and_1 (and_1_out, st___active, clock);
  // Probe on register_1_q
  Decoder #(.select(2), .enable("false")) decoder_1 (
    .out0(decoder_1_out0), .out1(decoder_1_out1), .out2(decoder_1_out2), .out3(decoder_1_out3),
    .sel(register_1_q));
  not not_1 (not_1_out, st___active);
  Adder #(.width(2)) adder_1 (.a(register_1_q), .b(2'b01), .out(adder_1_out));  // open: cin, cout
  Register #(.width(2)) register_1 (.D(adder_1_out), .Q(register_1_q), .clk(and_1_out), .clr(or_1_out));  // open: en
  or or_1 (or_1_out, not_1_out, reset);
  assign reg_out_addr1 = decoder_1_out1 ? src1 : 3'bz;  // Controlled_Buffer controlled_buffer_1
  assign alu_in1 = decoder_1_out1 ? reg_out1 : 16'bz;  // Controlled_Buffer controlled_buffer_2
  assign reg_out_addr2 = decoder_1_out1 ? src2 : 3'bz;  // Controlled_Buffer controlled_buffer_3
  assign alu_in_2 = decoder_1_out1 ? reg_out2 : 16'bz;  // Controlled_Buffer controlled_buffer_4
  assign alu_op = decoder_1_out1 ? 1'b0 : 1'bz;  // Controlled_Buffer controlled_buffer_5
  Multiplexer #(.enable("false")) multiplexer_1 (.in0(1'b0), .in1(1'b1), .out(alu_enable), .sel(decoder_1_out1));
  assign regz_in = decoder_1_out1 ? alu_out : 16'bz;  // Controlled_Buffer controlled_buffer_6
  assign regz_enable = decoder_1_out1 ? 1'b1 : 1'bz;  // Controlled_Buffer controlled_buffer_7
  // Probe on regz_out
  assign reg_in_add = decoder_1_out2 ? dest : 3'bz;  // Controlled_Buffer controlled_buffer_8
  assign reg_in = decoder_1_out2 ? regz_out : 16'bz;  // Controlled_Buffer controlled_buffer_9
  Multiplexer #(.enable("false")) multiplexer_2 (.in0(1'b0), .in1(1'b1), .out(reg_write), .sel(decoder_1_out2));
  assign fetch = decoder_1_out3 ? 1'b1 : 1'bz;  // Controlled_Buffer controlled_buffer_10

  // Other names for the same wires on the sheet: ALU_IN2[15:0] = alu_in_2; reg_out_add1[2:0] = reg_out_addr1;
  //   reg_out_add2[2:0] = reg_out_addr2
endmodule

// CMP
module cmp_state (
  input  [2:0] src1,
  input  [15:0] reg_out1,
  input  [2:0] dest,
  input  [15:0] regz_out,
  input  [2:0] src2,
  input  eq,
  input  [15:0] reg_out2,
  input  ls,
  input  gt,
  input  [15:0] alu_out,
  input  st___active,
  input  clock,
  input  reset,
  output [15:0] regz_in,
  output regz_enable,
  output [2:0] reg_out_addr1,
  output [2:0] reg_out_addr2,
  output [15:0] alu_in1,
  output [15:0] alu_in_2,
  output alu_op,
  output alu_enable,
  output [2:0] reg_in_add,
  output [15:0] reg_in,
  output reg_write,
  output fetch
);

  wire and_1_out, decoder_1_out0, decoder_1_out1, decoder_1_out2, decoder_1_out3, not_1_out, or_1_out;
  wire [1:0] adder_1_out, register_1_q;

  and and_1 (and_1_out, st___active, clock);
  // Probe on register_1_q
  Decoder #(.select(2), .enable("false")) decoder_1 (
    .out0(decoder_1_out0), .out1(decoder_1_out1), .out2(decoder_1_out2), .out3(decoder_1_out3),
    .sel(register_1_q));
  not not_1 (not_1_out, st___active);
  Adder #(.width(2)) adder_1 (.a(register_1_q), .b(2'b01), .out(adder_1_out));  // open: cin, cout
  Register #(.width(2)) register_1 (.D(adder_1_out), .Q(register_1_q), .clk(and_1_out), .clr(or_1_out));  // open: en
  or or_1 (or_1_out, not_1_out, reset);
  assign reg_out_addr1 = decoder_1_out1 ? src1 : 3'bz;  // Controlled_Buffer controlled_buffer_1
  assign alu_in1 = decoder_1_out1 ? reg_out1 : 16'bz;  // Controlled_Buffer controlled_buffer_2
  assign reg_out_addr2 = decoder_1_out1 ? src2 : 3'bz;  // Controlled_Buffer controlled_buffer_3
  assign alu_in_2 = decoder_1_out1 ? reg_out2 : 16'bz;  // Controlled_Buffer controlled_buffer_4
  assign alu_op = decoder_1_out1 ? 1'b0 : 1'bz;  // Controlled_Buffer controlled_buffer_5
  Multiplexer #(.enable("false")) multiplexer_1 (.in0(1'b0), .in1(1'b1), .out(alu_enable), .sel(decoder_1_out1));
  assign fetch = decoder_1_out2 ? 1'b1 : 1'bz;  // Controlled_Buffer controlled_buffer_6

  // Other names for the same wires on the sheet: ALU_IN2[15:0] = alu_in_2; reg_out_add1[2:0] = reg_out_addr1;
  //   reg_out_add2[2:0] = reg_out_addr2
endmodule

// jmp
module jmp_state (
  input  [9:0] address,
  input  alu_eq,
  input  alu_ls,
  input  alu_gt,
  input  st___active,
  input  clock,
  input  reset,
  output pc_enable,
  output [9:0] pc_addr,
  output pc_addr_select,
  output fetch
);

  wire and_1_out, decoder_1_out0, decoder_1_out1, decoder_1_out2, decoder_1_out3, not_1_out, or_1_out;
  wire [1:0] adder_1_out, register_1_q;
  wire [9:0] multiplexer_1_out;

  and and_1 (and_1_out, st___active, clock);
  // Probe on register_1_q
  Decoder #(.select(2), .enable("false")) decoder_1 (
    .out0(decoder_1_out0), .out1(decoder_1_out1), .out2(decoder_1_out2), .out3(decoder_1_out3),
    .sel(register_1_q));
  not not_1 (not_1_out, st___active);
  Adder #(.width(2)) adder_1 (.a(register_1_q), .b(2'b01), .out(adder_1_out));  // open: cin, cout
  Multiplexer #(.width(10), .enable("false")) multiplexer_1 (
    .in0({10{1'b0}}), .in1(address), .out(multiplexer_1_out), .sel(decoder_1_out1));
  Register #(.width(2)) register_1 (.D(adder_1_out), .Q(register_1_q), .clk(and_1_out), .clr(or_1_out));  // open: en
  or or_1 (or_1_out, not_1_out, reset);
  assign pc_enable = decoder_1_out1 ? 1'b1 : 1'bz;  // Controlled_Buffer controlled_buffer_1
  assign pc_addr = decoder_1_out1 ? multiplexer_1_out : 10'bz;  // Controlled_Buffer controlled_buffer_2
  assign pc_addr_select = decoder_1_out1 ? 1'b1 : 1'bz;  // Controlled_Buffer controlled_buffer_3
  assign fetch = decoder_1_out2 ? 1'b1 : 1'bz;  // Controlled_Buffer controlled_buffer_4
endmodule

// ja
module ja_state (
  input  [9:0] address,
  input  alu_eq,
  input  alu_ls,
  input  alu_gt,
  input  st___active,
  input  clock,
  input  reset,
  output pc_enable,
  output [9:0] pc_addr,
  output pc_addr_select,
  output fetch
);

  wire and_1_out, decoder_1_out0, decoder_1_out1, decoder_1_out2, decoder_1_out3, not_1_out, or_1_out;
  wire [1:0] adder_1_out, register_1_q;
  wire [9:0] multiplexer_1_out;

  and and_1 (and_1_out, st___active, clock);
  // Probe on register_1_q
  Decoder #(.select(2), .enable("false")) decoder_1 (
    .out0(decoder_1_out0), .out1(decoder_1_out1), .out2(decoder_1_out2), .out3(decoder_1_out3),
    .sel(register_1_q));
  not not_1 (not_1_out, st___active);
  Adder #(.width(2)) adder_1 (.a(register_1_q), .b(2'b01), .out(adder_1_out));  // open: cin, cout
  Multiplexer #(.width(10), .enable("false")) multiplexer_1 (
    .in0({10{1'b0}}), .in1(address), .out(multiplexer_1_out), .sel(alu_gt));
  Register #(.width(2)) register_1 (.D(adder_1_out), .Q(register_1_q), .clk(and_1_out), .clr(or_1_out));  // open: en
  or or_1 (or_1_out, not_1_out, reset);
  assign pc_enable = decoder_1_out1 ? 1'b1 : 1'bz;  // Controlled_Buffer controlled_buffer_1
  assign pc_addr = decoder_1_out1 ? multiplexer_1_out : 10'bz;  // Controlled_Buffer controlled_buffer_2
  assign pc_addr_select = decoder_1_out1 ? 1'b1 : 1'bz;  // Controlled_Buffer controlled_buffer_3
  assign fetch = decoder_1_out2 ? 1'b1 : 1'bz;  // Controlled_Buffer controlled_buffer_4
endmodule

// jae
module jae_state (
  input  [9:0] address,
  input  alu_eq,
  input  alu_ls,
  input  alu_gt,
  input  st___active,
  input  clock,
  input  reset,
  output pc_enable,
  output [9:0] pc_addr,
  output pc_addr_select,
  output fetch
);

  wire and_1_out, decoder_1_out0, decoder_1_out1, decoder_1_out2, decoder_1_out3, not_1_out, or_1_out,
       or_2_out;
  wire [1:0] adder_1_out, register_1_q;
  wire [9:0] multiplexer_1_out;

  and and_1 (and_1_out, st___active, clock);
  // Probe on register_1_q
  Decoder #(.select(2), .enable("false")) decoder_1 (
    .out0(decoder_1_out0), .out1(decoder_1_out1), .out2(decoder_1_out2), .out3(decoder_1_out3),
    .sel(register_1_q));
  not not_1 (not_1_out, st___active);
  Adder #(.width(2)) adder_1 (.a(register_1_q), .b(2'b01), .out(adder_1_out));  // open: cin, cout
  Multiplexer #(.width(10), .enable("false")) multiplexer_1 (
    .in0({10{1'b0}}), .in1(address), .out(multiplexer_1_out), .sel(or_1_out));
  or or_1 (or_1_out, alu_gt, alu_eq);
  Register #(.width(2)) register_1 (.D(adder_1_out), .Q(register_1_q), .clk(and_1_out), .clr(or_2_out));  // open: en
  or or_2 (or_2_out, not_1_out, reset);
  assign pc_enable = decoder_1_out1 ? 1'b1 : 1'bz;  // Controlled_Buffer controlled_buffer_1
  assign pc_addr = decoder_1_out1 ? multiplexer_1_out : 10'bz;  // Controlled_Buffer controlled_buffer_2
  assign pc_addr_select = decoder_1_out1 ? 1'b1 : 1'bz;  // Controlled_Buffer controlled_buffer_3
  assign fetch = decoder_1_out2 ? 1'b1 : 1'bz;  // Controlled_Buffer controlled_buffer_4
endmodule

// je
module je_state (
  input  [9:0] address,
  input  alu_eq,
  input  alu_ls,
  input  alu_gt,
  input  st___active,
  input  clock,
  input  reset,
  output pc_enable,
  output [9:0] pc_addr,
  output pc_addr_select,
  output fetch
);

  wire and_1_out, decoder_1_out0, decoder_1_out1, decoder_1_out2, decoder_1_out3, not_1_out, or_1_out;
  wire [1:0] adder_1_out, register_1_q;
  wire [9:0] multiplexer_1_out;

  and and_1 (and_1_out, st___active, clock);
  // Probe on register_1_q
  Decoder #(.select(2), .enable("false")) decoder_1 (
    .out0(decoder_1_out0), .out1(decoder_1_out1), .out2(decoder_1_out2), .out3(decoder_1_out3),
    .sel(register_1_q));
  not not_1 (not_1_out, st___active);
  Adder #(.width(2)) adder_1 (.a(register_1_q), .b(2'b01), .out(adder_1_out));  // open: cin, cout
  Multiplexer #(.width(10), .enable("false")) multiplexer_1 (
    .in0({10{1'b0}}), .in1(address), .out(multiplexer_1_out), .sel(alu_eq));
  Register #(.width(2)) register_1 (.D(adder_1_out), .Q(register_1_q), .clk(and_1_out), .clr(or_1_out));  // open: en
  or or_1 (or_1_out, not_1_out, reset);
  assign pc_enable = decoder_1_out1 ? 1'b1 : 1'bz;  // Controlled_Buffer controlled_buffer_1
  assign pc_addr = decoder_1_out1 ? multiplexer_1_out : 10'bz;  // Controlled_Buffer controlled_buffer_2
  assign pc_addr_select = decoder_1_out1 ? 1'b1 : 1'bz;  // Controlled_Buffer controlled_buffer_3
  assign fetch = decoder_1_out2 ? 1'b1 : 1'bz;  // Controlled_Buffer controlled_buffer_4
endmodule

// jb
module jb_state (
  input  [9:0] address,
  input  alu_eq,
  input  alu_ls,
  input  alu_gt,
  input  st___active,
  input  clock,
  input  reset,
  output pc_enable,
  output [9:0] pc_addr,
  output pc_addr_select,
  output fetch
);

  wire and_1_out, decoder_1_out0, decoder_1_out1, decoder_1_out2, decoder_1_out3, not_1_out, or_1_out;
  wire [1:0] adder_1_out, register_1_q;
  wire [9:0] multiplexer_1_out;

  and and_1 (and_1_out, st___active, clock);
  // Probe on register_1_q
  Decoder #(.select(2), .enable("false")) decoder_1 (
    .out0(decoder_1_out0), .out1(decoder_1_out1), .out2(decoder_1_out2), .out3(decoder_1_out3),
    .sel(register_1_q));
  not not_1 (not_1_out, st___active);
  Adder #(.width(2)) adder_1 (.a(register_1_q), .b(2'b01), .out(adder_1_out));  // open: cin, cout
  Multiplexer #(.width(10), .enable("false")) multiplexer_1 (
    .in0({10{1'b0}}), .in1(address), .out(multiplexer_1_out), .sel(alu_ls));
  Register #(.width(2)) register_1 (.D(adder_1_out), .Q(register_1_q), .clk(and_1_out), .clr(or_1_out));  // open: en
  or or_1 (or_1_out, not_1_out, reset);
  assign pc_enable = decoder_1_out1 ? 1'b1 : 1'bz;  // Controlled_Buffer controlled_buffer_1
  assign pc_addr = decoder_1_out1 ? multiplexer_1_out : 10'bz;  // Controlled_Buffer controlled_buffer_2
  assign pc_addr_select = decoder_1_out1 ? 1'b1 : 1'bz;  // Controlled_Buffer controlled_buffer_3
  assign fetch = decoder_1_out2 ? 1'b1 : 1'bz;  // Controlled_Buffer controlled_buffer_4
endmodule

// jbe
module jbe_state (
  input  [9:0] address,
  input  alu_eq,
  input  alu_ls,
  input  alu_gt,
  input  st___active,
  input  clock,
  input  reset,
  output pc_enable,
  output [9:0] pc_addr,
  output pc_addr_select,
  output fetch
);

  wire and_1_out, decoder_1_out0, decoder_1_out1, decoder_1_out2, decoder_1_out3, not_1_out, or_1_out,
       or_2_out;
  wire [1:0] adder_1_out, register_1_q;
  wire [9:0] multiplexer_1_out;

  and and_1 (and_1_out, st___active, clock);
  // Probe on register_1_q
  Decoder #(.select(2), .enable("false")) decoder_1 (
    .out0(decoder_1_out0), .out1(decoder_1_out1), .out2(decoder_1_out2), .out3(decoder_1_out3),
    .sel(register_1_q));
  not not_1 (not_1_out, st___active);
  // Probe on address
  Adder #(.width(2)) adder_1 (.a(register_1_q), .b(2'b01), .out(adder_1_out));  // open: cin, cout
  Multiplexer #(.width(10), .enable("false")) multiplexer_1 (
    .in0({10{1'b0}}), .in1(address), .out(multiplexer_1_out), .sel(or_1_out));
  or or_1 (or_1_out, alu_eq, alu_ls);
  Register #(.width(2)) register_1 (.D(adder_1_out), .Q(register_1_q), .clk(and_1_out), .clr(or_2_out));  // open: en
  or or_2 (or_2_out, not_1_out, reset);
  assign pc_enable = decoder_1_out1 ? 1'b1 : 1'bz;  // Controlled_Buffer controlled_buffer_1
  // Probe on pc_addr
  assign pc_addr = decoder_1_out1 ? multiplexer_1_out : 10'bz;  // Controlled_Buffer controlled_buffer_2
  assign pc_addr_select = decoder_1_out1 ? 1'b1 : 1'bz;  // Controlled_Buffer controlled_buffer_3
  assign fetch = decoder_1_out2 ? 1'b1 : 1'bz;  // Controlled_Buffer controlled_buffer_4
endmodule
